// Logisim project ALU_32bit.circ as structural Verilog: 5 circuits, main circuit ALU_32bit
module ALU_32bit (
  input  [4:0] ALUControl,
  input  [31:0] SrcA,
  input  [31:0] SrcB,
  output Zero,
  output [31:0] ALUResult,
  output Cout
);

  wire [31:0] and_1_out, bit_extender_1_out, multiplexer_1_out, nor_1_out, not_1_out, or_1_out,
       prefix_adder_32bit_1_s, shifter_1_out, shifter_2_out, shifter_3_out, shifter_4_out, xor_1_out;

  assign not_1_out = ~SrcB;  // NOT_Gate not_1, 32 bits wide
  Multiplexer #(.width(32)) multiplexer_1 (.in0(SrcB), .in1(not_1_out), .out(multiplexer_1_out), .sel(ALUControl[4]));
  assign and_1_out = SrcA & multiplexer_1_out;  // AND_Gate and_1, 32 bits wide
  assign or_1_out = multiplexer_1_out | SrcA;  // OR_Gate or_1, 32 bits wide
  assign xor_1_out = multiplexer_1_out ^ SrcA;  // XOR_Gate xor_1, 32 bits wide
  assign nor_1_out = ~(multiplexer_1_out | SrcA);  // NOR_Gate nor_1, 32 bits wide
  Shifter #(.width(32)) shifter_1 (.in(multiplexer_1_out), .\dist (SrcA[4:0]), .out(shifter_1_out));
  Shifter #(.shift("lr"), .width(32)) shifter_2 (.in(multiplexer_1_out), .\dist (SrcA[4:0]), .out(shifter_2_out));
  Shifter #(.shift("ar"), .width(32)) shifter_3 (.in(multiplexer_1_out), .\dist (SrcA[4:0]), .out(shifter_3_out));
  Shifter #(.width(32)) shifter_4 (.in(multiplexer_1_out), .\dist (5'b10000), .out(shifter_4_out));
  Prefix_Adder_32bit prefix_adder_32bit_1 (
    .Cin(ALUControl[4]), .B(multiplexer_1_out), .A(SrcA), .Cout(Cout), .S(prefix_adder_32bit_1_s));
  assign bit_extender_1_out = {{31{1'b0}}, prefix_adder_32bit_1_s[31]};  // Bit_Extender bit_extender_1
  Multiplexer #(.select(4), .width(32)) multiplexer_2 (
    .in0(and_1_out), .in1(or_1_out), .in2(prefix_adder_32bit_1_s), .in3(bit_extender_1_out), .in4(xor_1_out),
    .in5(nor_1_out), .in6(shifter_1_out), .in7(shifter_2_out), .in8(shifter_3_out), .in9(shifter_4_out),
    .out(ALUResult));  // open: in10, in11, in12, in13, in14, in15, sel
  nor nor_2 (Zero, ALUResult[0], ALUResult[1], ALUResult[2], ALUResult[3], ALUResult[4], ALUResult[5], ALUResult[6], ALUResult[7], ALUResult[8], ALUResult[9], ALUResult[10], ALUResult[11], ALUResult[12], ALUResult[13], ALUResult[14], ALUResult[15], ALUResult[17], ALUResult[18], ALUResult[19], ALUResult[20], ALUResult[21], ALUResult[22], ALUResult[23], ALUResult[24], ALUResult[25], ALUResult[26], ALUResult[27], ALUResult[28], ALUResult[29], ALUResult[30], ALUResult[31]);
endmodule

module Black_Cell (
  input  Gu,
  input  Gl,
  input  Pu,
  input  Pl,
  output G,
  output P
);

  wire and_1_out;

  and and_1 (and_1_out, Gl, Pu);
  and and_2 (P, Pu, Pl);
  or or_1 (G, and_1_out, Gu);
endmodule

module Step_1 (
  input  A,
  input  B,
  output G,
  output P
);

  and and_1 (G, A, B);
  or or_1 (P, A, B);
endmodule

module Sum (
  input  A,
  input  B,
  input  G,
  output S
);

  wire xor_1_out;

  xor xor_1 (xor_1_out, A, B);
  xor xor_2 (S, xor_1_out, G);
endmodule

module Prefix_Adder_32bit (
  input  Cin,
  input  [31:0] B,
  input  [31:0] A,
  output Cout,
  output [31:0] S
);

  wire black_cell_1_g, black_cell_1_p, black_cell_2_g, black_cell_2_p, black_cell_3_g, black_cell_3_p,
       black_cell_4_g, black_cell_4_p, black_cell_5_g, black_cell_5_p, black_cell_6_g, black_cell_6_p,
       black_cell_7_g, black_cell_7_p, black_cell_8_g, black_cell_8_p, black_cell_9_g, black_cell_9_p,
       black_cell_10_g, black_cell_10_p, black_cell_11_g, black_cell_11_p, black_cell_12_g, black_cell_12_p,
       black_cell_13_g, black_cell_13_p, black_cell_14_g, black_cell_14_p, black_cell_15_g, black_cell_15_p,
       black_cell_16_g, black_cell_16_p, black_cell_17_g, black_cell_18_g, black_cell_18_p, black_cell_19_g,
       black_cell_19_p, black_cell_20_g, black_cell_20_p, black_cell_21_g, black_cell_21_p, black_cell_22_g,
       black_cell_22_p, black_cell_23_g, black_cell_23_p, black_cell_24_g, black_cell_24_p, black_cell_25_g,
       black_cell_25_p, black_cell_26_g, black_cell_26_p, black_cell_27_g, black_cell_27_p, black_cell_28_g,
       black_cell_28_p, black_cell_29_g, black_cell_29_p, black_cell_30_g, black_cell_30_p, black_cell_31_g,
       black_cell_31_p, black_cell_32_g, black_cell_32_p, black_cell_33_g, black_cell_34_g, black_cell_35_g,
       black_cell_36_g, black_cell_36_p, black_cell_37_g, black_cell_37_p, black_cell_38_g, black_cell_38_p,
       black_cell_39_g, black_cell_39_p, black_cell_40_g, black_cell_40_p, black_cell_41_g, black_cell_41_p,
       black_cell_42_g, black_cell_42_p, black_cell_43_g, black_cell_43_p, black_cell_44_g, black_cell_44_p,
       black_cell_45_g, black_cell_45_p, black_cell_46_g, black_cell_46_p, black_cell_47_g, black_cell_47_p,
       black_cell_48_g, black_cell_48_p, black_cell_49_g, black_cell_50_g, black_cell_51_g, black_cell_52_g,
       black_cell_53_g, black_cell_54_g, black_cell_55_g, black_cell_56_g, black_cell_56_p, black_cell_57_g,
       black_cell_57_p, black_cell_58_g, black_cell_58_p, black_cell_59_g, black_cell_59_p, black_cell_60_g,
       black_cell_60_p, black_cell_61_g, black_cell_61_p, black_cell_62_g, black_cell_62_p, black_cell_63_g,
       black_cell_63_p, black_cell_64_g, black_cell_64_p, black_cell_65_g, black_cell_66_g, black_cell_67_g,
       black_cell_68_g, black_cell_69_g, black_cell_70_g, black_cell_71_g, black_cell_72_g, black_cell_73_g,
       black_cell_74_g, black_cell_75_g, black_cell_76_g, black_cell_77_g, black_cell_78_g, black_cell_79_g,
       black_cell_80_g, black_cell_80_p, step_1_1_g, step_1_1_p, step_1_2_g, step_1_2_p, step_1_3_g,
       step_1_3_p, step_1_4_g, step_1_4_p, step_1_5_g, step_1_5_p, step_1_6_g, step_1_6_p, step_1_7_g,
       step_1_7_p, step_1_8_g, step_1_8_p, step_1_9_g, step_1_9_p, step_1_10_g, step_1_10_p, step_1_11_g,
       step_1_11_p, step_1_12_g, step_1_12_p, step_1_13_g, step_1_13_p, step_1_14_g, step_1_14_p,
       step_1_15_g, step_1_15_p, step_1_16_g, step_1_16_p, step_1_17_g, step_1_17_p, step_1_18_g,
       step_1_18_p, step_1_19_g, step_1_19_p, step_1_20_g, step_1_20_p, step_1_21_g, step_1_21_p,
       step_1_22_g, step_1_22_p, step_1_23_g, step_1_23_p, step_1_24_g, step_1_24_p, step_1_25_g,
       step_1_25_p, step_1_26_g, step_1_26_p, step_1_27_g, step_1_27_p, step_1_28_g, step_1_28_p,
       step_1_29_g, step_1_29_p, step_1_30_g, step_1_30_p, step_1_31_g, step_1_31_p, step_1_32_g,
       step_1_32_p, step_1_33_g, step_1_33_p;

  Step_1 step_1_1 (.A(Cin), .B(Cin), .G(step_1_1_g), .P(step_1_1_p));
  Step_1 step_1_2 (.A(A[0]), .B(B[0]), .G(step_1_2_g), .P(step_1_2_p));
  Step_1 step_1_3 (.A(A[1]), .B(B[1]), .G(step_1_3_g), .P(step_1_3_p));
  Step_1 step_1_4 (.A(A[2]), .B(B[2]), .G(step_1_4_g), .P(step_1_4_p));
  Step_1 step_1_5 (.A(A[3]), .B(B[3]), .G(step_1_5_g), .P(step_1_5_p));
  Step_1 step_1_6 (.A(A[4]), .B(B[4]), .G(step_1_6_g), .P(step_1_6_p));
  Step_1 step_1_7 (.A(A[5]), .B(B[5]), .G(step_1_7_g), .P(step_1_7_p));
  Step_1 step_1_8 (.A(A[6]), .B(B[6]), .G(step_1_8_g), .P(step_1_8_p));
  Step_1 step_1_9 (.A(A[7]), .B(B[7]), .G(step_1_9_g), .P(step_1_9_p));
  Step_1 step_1_10 (.A(A[8]), .B(B[8]), .G(step_1_10_g), .P(step_1_10_p));
  Step_1 step_1_11 (.A(A[9]), .B(B[9]), .G(step_1_11_g), .P(step_1_11_p));
  Step_1 step_1_12 (.A(A[10]), .B(B[10]), .G(step_1_12_g), .P(step_1_12_p));
  Step_1 step_1_13 (.A(A[11]), .B(B[11]), .G(step_1_13_g), .P(step_1_13_p));
  Step_1 step_1_14 (.A(A[12]), .B(B[12]), .G(step_1_14_g), .P(step_1_14_p));
  Step_1 step_1_15 (.A(A[13]), .B(B[13]), .G(step_1_15_g), .P(step_1_15_p));
  Step_1 step_1_16 (.A(A[14]), .B(B[14]), .G(step_1_16_g), .P(step_1_16_p));
  Step_1 step_1_17 (.A(A[15]), .B(B[15]), .G(step_1_17_g), .P(step_1_17_p));
  Step_1 step_1_18 (.A(A[16]), .B(B[16]), .G(step_1_18_g), .P(step_1_18_p));
  Step_1 step_1_19 (.A(A[17]), .B(B[17]), .G(step_1_19_g), .P(step_1_19_p));
  Step_1 step_1_20 (.A(A[18]), .B(B[18]), .G(step_1_20_g), .P(step_1_20_p));
  Step_1 step_1_21 (.A(A[19]), .B(B[19]), .G(step_1_21_g), .P(step_1_21_p));
  Step_1 step_1_22 (.A(A[20]), .B(B[20]), .G(step_1_22_g), .P(step_1_22_p));
  Step_1 step_1_23 (.A(A[21]), .B(B[21]), .G(step_1_23_g), .P(step_1_23_p));
  Step_1 step_1_24 (.A(A[22]), .B(B[22]), .G(step_1_24_g), .P(step_1_24_p));
  Step_1 step_1_25 (.A(A[23]), .B(B[23]), .G(step_1_25_g), .P(step_1_25_p));
  Step_1 step_1_26 (.A(A[24]), .B(B[24]), .G(step_1_26_g), .P(step_1_26_p));
  Step_1 step_1_27 (.A(A[25]), .B(B[25]), .G(step_1_27_g), .P(step_1_27_p));
  Step_1 step_1_28 (.A(A[26]), .B(B[26]), .G(step_1_28_g), .P(step_1_28_p));
  Step_1 step_1_29 (.A(A[27]), .B(B[27]), .G(step_1_29_g), .P(step_1_29_p));
  Step_1 step_1_30 (.A(A[28]), .B(B[28]), .G(step_1_30_g), .P(step_1_30_p));
  Step_1 step_1_31 (.A(A[29]), .B(B[29]), .G(step_1_31_g), .P(step_1_31_p));
  Step_1 step_1_32 (.A(A[30]), .B(B[30]), .G(step_1_32_g), .P(step_1_32_p));
  Step_1 step_1_33 (.A(A[31]), .B(B[31]), .G(step_1_33_g), .P(step_1_33_p));
  Black_Cell black_cell_1 (
    .Gu(step_1_2_g), .Gl(step_1_1_g), .Pu(step_1_2_p), .Pl(step_1_1_p), .G(black_cell_1_g), .P(black_cell_1_p));
  Black_Cell black_cell_2 (
    .Gu(step_1_4_g), .Gl(step_1_3_g), .Pu(step_1_4_p), .Pl(step_1_3_p), .G(black_cell_2_g), .P(black_cell_2_p));
  Black_Cell black_cell_3 (
    .Gu(step_1_6_g), .Gl(step_1_5_g), .Pu(step_1_6_p), .Pl(step_1_5_p), .G(black_cell_3_g), .P(black_cell_3_p));
  Black_Cell black_cell_4 (
    .Gu(step_1_8_g), .Gl(step_1_7_g), .Pu(step_1_8_p), .Pl(step_1_7_p), .G(black_cell_4_g), .P(black_cell_4_p));
  Black_Cell black_cell_5 (
    .Gu(step_1_10_g), .Gl(step_1_9_g), .Pu(step_1_10_p), .Pl(step_1_9_p), .G(black_cell_5_g),
    .P(black_cell_5_p));
  Black_Cell black_cell_6 (
    .Gu(step_1_12_g), .Gl(step_1_11_g), .Pu(step_1_12_p), .Pl(step_1_11_p), .G(black_cell_6_g),
    .P(black_cell_6_p));
  Black_Cell black_cell_7 (
    .Gu(step_1_14_g), .Gl(step_1_13_g), .Pu(step_1_14_p), .Pl(step_1_13_p), .G(black_cell_7_g),
    .P(black_cell_7_p));
  Black_Cell black_cell_8 (
    .Gu(step_1_16_g), .Gl(step_1_15_g), .Pu(step_1_16_p), .Pl(step_1_15_p), .G(black_cell_8_g),
    .P(black_cell_8_p));
  Black_Cell black_cell_9 (
    .Gu(step_1_18_g), .Gl(step_1_17_g), .Pu(step_1_18_p), .Pl(step_1_17_p), .G(black_cell_9_g),
    .P(black_cell_9_p));
  Black_Cell black_cell_10 (
    .Gu(step_1_20_g), .Gl(step_1_19_g), .Pu(step_1_20_p), .Pl(step_1_19_p), .G(black_cell_10_g),
    .P(black_cell_10_p));
  Black_Cell black_cell_11 (
    .Gu(step_1_22_g), .Gl(step_1_21_g), .Pu(step_1_22_p), .Pl(step_1_21_p), .G(black_cell_11_g),
    .P(black_cell_11_p));
  Black_Cell black_cell_12 (
    .Gu(step_1_24_g), .Gl(step_1_23_g), .Pu(step_1_24_p), .Pl(step_1_23_p), .G(black_cell_12_g),
    .P(black_cell_12_p));
  Black_Cell black_cell_13 (
    .Gu(step_1_26_g), .Gl(step_1_25_g), .Pu(step_1_26_p), .Pl(step_1_25_p), .G(black_cell_13_g),
    .P(black_cell_13_p));
  Black_Cell black_cell_14 (
    .Gu(step_1_28_g), .Gl(step_1_27_g), .Pu(step_1_28_p), .Pl(step_1_27_p), .G(black_cell_14_g),
    .P(black_cell_14_p));
  Black_Cell black_cell_15 (
    .Gu(step_1_30_g), .Gl(step_1_29_g), .Pu(step_1_30_p), .Pl(step_1_29_p), .G(black_cell_15_g),
    .P(black_cell_15_p));
  Black_Cell black_cell_16 (
    .Gu(step_1_32_g), .Gl(step_1_31_g), .Pu(step_1_32_p), .Pl(step_1_31_p), .G(black_cell_16_g),
    .P(black_cell_16_p));
  Black_Cell black_cell_17 (
    .Gu(step_1_3_g), .Gl(black_cell_1_g), .Pu(step_1_3_p), .Pl(black_cell_1_p), .G(black_cell_17_g));  // open: P
  Black_Cell black_cell_18 (
    .Gu(black_cell_2_g), .Gl(black_cell_1_g), .Pu(black_cell_2_p), .Pl(black_cell_1_p), .G(black_cell_18_g),
    .P(black_cell_18_p));
  Black_Cell black_cell_19 (
    .Gu(step_1_7_g), .Gl(black_cell_3_g), .Pu(step_1_7_p), .Pl(black_cell_3_p), .G(black_cell_19_g),
    .P(black_cell_19_p));
  Black_Cell black_cell_20 (
    .Gu(black_cell_4_g), .Gl(black_cell_3_g), .Pu(black_cell_4_p), .Pl(black_cell_3_p), .G(black_cell_20_g),
    .P(black_cell_20_p));
  Black_Cell black_cell_21 (
    .Gu(step_1_11_g), .Gl(black_cell_5_g), .Pu(step_1_11_p), .Pl(black_cell_5_p), .G(black_cell_21_g),
    .P(black_cell_21_p));
  Black_Cell black_cell_22 (
    .Gu(black_cell_6_g), .Gl(black_cell_5_g), .Pu(black_cell_6_p), .Pl(black_cell_5_p), .G(black_cell_22_g),
    .P(black_cell_22_p));
  Black_Cell black_cell_23 (
    .Gu(step_1_15_g), .Gl(black_cell_7_g), .Pu(step_1_15_p), .Pl(black_cell_7_p), .G(black_cell_23_g),
    .P(black_cell_23_p));
  Black_Cell black_cell_24 (
    .Gu(black_cell_8_g), .Gl(black_cell_7_g), .Pu(black_cell_8_p), .Pl(black_cell_7_p), .G(black_cell_24_g),
    .P(black_cell_24_p));
  Black_Cell black_cell_25 (
    .Gu(step_1_19_g), .Gl(black_cell_9_g), .Pu(step_1_19_p), .Pl(black_cell_9_p), .G(black_cell_25_g),
    .P(black_cell_25_p));
  Black_Cell black_cell_26 (
    .Gu(black_cell_10_g), .Gl(black_cell_9_g), .Pu(black_cell_10_p), .Pl(black_cell_9_p),
    .G(black_cell_26_g), .P(black_cell_26_p));
  Black_Cell black_cell_27 (
    .Gu(step_1_23_g), .Gl(black_cell_11_g), .Pu(step_1_23_p), .Pl(black_cell_11_p), .G(black_cell_27_g),
    .P(black_cell_27_p));
  Black_Cell black_cell_28 (
    .Gu(black_cell_12_g), .Gl(black_cell_11_g), .Pu(black_cell_12_p), .Pl(black_cell_11_p),
    .G(black_cell_28_g), .P(black_cell_28_p));
  Black_Cell black_cell_29 (
    .Gu(step_1_27_g), .Gl(black_cell_13_g), .Pu(step_1_27_p), .Pl(black_cell_13_p), .G(black_cell_29_g),
    .P(black_cell_29_p));
  Black_Cell black_cell_30 (
    .Gu(black_cell_14_g), .Gl(black_cell_13_g), .Pu(black_cell_14_p), .Pl(black_cell_13_p),
    .G(black_cell_30_g), .P(black_cell_30_p));
  Black_Cell black_cell_31 (
    .Gu(step_1_31_g), .Gl(black_cell_15_g), .Pu(step_1_31_p), .Pl(black_cell_15_p), .G(black_cell_31_g),
    .P(black_cell_31_p));
  Black_Cell black_cell_32 (
    .Gu(black_cell_16_g), .Gl(black_cell_15_g), .Pu(black_cell_16_p), .Pl(black_cell_15_p),
    .G(black_cell_32_g), .P(black_cell_32_p));
  Black_Cell black_cell_33 (
    .Gu(step_1_5_g), .Gl(black_cell_18_g), .Pu(step_1_5_p), .Pl(black_cell_18_p), .G(black_cell_33_g));  // open: P
  Black_Cell black_cell_34 (
    .Gu(black_cell_3_g), .Gl(black_cell_18_g), .Pu(black_cell_3_p), .Pl(black_cell_18_p), .G(black_cell_34_g));  // open: P
  Black_Cell black_cell_35 (
    .Gu(black_cell_19_g), .Gl(black_cell_18_g), .Pu(black_cell_19_p), .Pl(black_cell_18_p),
    .G(black_cell_35_g));  // open: P
  Black_Cell black_cell_36 (
    .Gu(black_cell_20_g), .Gl(black_cell_18_g), .Pu(black_cell_20_p), .Pl(black_cell_18_p),
    .G(black_cell_36_g), .P(black_cell_36_p));
  Black_Cell black_cell_37 (
    .Gu(step_1_13_g), .Gl(black_cell_22_g), .Pu(step_1_13_p), .Pl(black_cell_22_p), .G(black_cell_37_g),
    .P(black_cell_37_p));
  Black_Cell black_cell_38 (
    .Gu(black_cell_7_g), .Gl(black_cell_22_g), .Pu(black_cell_7_p), .Pl(black_cell_22_p),
    .G(black_cell_38_g), .P(black_cell_38_p));
  Black_Cell black_cell_39 (
    .Gu(black_cell_23_g), .Gl(black_cell_22_g), .Pu(black_cell_23_p), .Pl(black_cell_22_p),
    .G(black_cell_39_g), .P(black_cell_39_p));
  Black_Cell black_cell_40 (
    .Gu(black_cell_24_g), .Gl(black_cell_22_g), .Pu(black_cell_24_p), .Pl(black_cell_22_p),
    .G(black_cell_40_g), .P(black_cell_40_p));
  Black_Cell black_cell_41 (
    .Gu(step_1_21_g), .Gl(black_cell_26_g), .Pu(step_1_21_p), .Pl(black_cell_26_p), .G(black_cell_41_g),
    .P(black_cell_41_p));
  Black_Cell black_cell_42 (
    .Gu(black_cell_11_g), .Gl(black_cell_26_g), .Pu(black_cell_11_p), .Pl(black_cell_26_p),
    .G(black_cell_42_g), .P(black_cell_42_p));
  Black_Cell black_cell_43 (
    .Gu(black_cell_27_g), .Gl(black_cell_26_g), .Pu(black_cell_27_p), .Pl(black_cell_26_p),
    .G(black_cell_43_g), .P(black_cell_43_p));
  Black_Cell black_cell_44 (
    .Gu(black_cell_28_g), .Gl(black_cell_26_g), .Pu(black_cell_28_p), .Pl(black_cell_26_p),
    .G(black_cell_44_g), .P(black_cell_44_p));
  Black_Cell black_cell_45 (
    .Gu(step_1_29_g), .Gl(black_cell_30_g), .Pu(step_1_29_p), .Pl(black_cell_30_p), .G(black_cell_45_g),
    .P(black_cell_45_p));
  Black_Cell black_cell_46 (
    .Gu(black_cell_15_g), .Gl(black_cell_30_g), .Pu(black_cell_15_p), .Pl(black_cell_30_p),
    .G(black_cell_46_g), .P(black_cell_46_p));
  Black_Cell black_cell_47 (
    .Gu(black_cell_31_g), .Gl(black_cell_30_g), .Pu(black_cell_31_p), .Pl(black_cell_30_p),
    .G(black_cell_47_g), .P(black_cell_47_p));
  Black_Cell black_cell_48 (
    .Gu(black_cell_32_g), .Gl(black_cell_30_g), .Pu(black_cell_32_p), .Pl(black_cell_30_p),
    .G(black_cell_48_g), .P(black_cell_48_p));
  Black_Cell black_cell_49 (
    .Gu(step_1_9_g), .Gl(black_cell_36_g), .Pu(step_1_9_p), .Pl(black_cell_36_p), .G(black_cell_49_g));  // open: P
  Black_Cell black_cell_50 (
    .Gu(black_cell_5_g), .Gl(black_cell_36_g), .Pu(black_cell_5_p), .Pl(black_cell_36_p), .G(black_cell_50_g));  // open: P
  Black_Cell black_cell_51 (
    .Gu(black_cell_21_g), .Gl(black_cell_36_g), .Pu(black_cell_21_p), .Pl(black_cell_36_p),
    .G(black_cell_51_g));  // open: P
  Black_Cell black_cell_52 (
    .Gu(black_cell_22_g), .Gl(black_cell_36_g), .Pu(black_cell_22_p), .Pl(black_cell_36_p),
    .G(black_cell_52_g));  // open: P
  Black_Cell black_cell_53 (
    .Gu(black_cell_37_g), .Gl(black_cell_36_g), .Pu(black_cell_37_p), .Pl(black_cell_36_p),
    .G(black_cell_53_g));  // open: P
  Black_Cell black_cell_54 (
    .Gu(black_cell_38_g), .Gl(black_cell_36_g), .Pu(black_cell_38_p), .Pl(black_cell_36_p),
    .G(black_cell_54_g));  // open: P
  Black_Cell black_cell_55 (
    .Gu(black_cell_39_g), .Gl(black_cell_36_g), .Pu(black_cell_39_p), .Pl(black_cell_36_p),
    .G(black_cell_55_g));  // open: P
  Black_Cell black_cell_56 (
    .Gu(black_cell_40_g), .Gl(black_cell_36_g), .Pu(black_cell_40_p), .Pl(black_cell_36_p),
    .G(black_cell_56_g), .P(black_cell_56_p));
  Black_Cell black_cell_57 (
    .Gu(step_1_25_g), .Gl(black_cell_44_g), .Pu(step_1_25_p), .Pl(black_cell_44_p), .G(black_cell_57_g),
    .P(black_cell_57_p));
  Black_Cell black_cell_58 (
    .Gu(black_cell_13_g), .Gl(black_cell_44_g), .Pu(black_cell_13_p), .Pl(black_cell_44_p),
    .G(black_cell_58_g), .P(black_cell_58_p));
  Black_Cell black_cell_59 (
    .Gu(black_cell_29_g), .Gl(black_cell_44_g), .Pu(black_cell_29_p), .Pl(black_cell_44_p),
    .G(black_cell_59_g), .P(black_cell_59_p));
  Black_Cell black_cell_60 (
    .Gu(black_cell_30_g), .Gl(black_cell_44_g), .Pu(black_cell_30_p), .Pl(black_cell_44_p),
    .G(black_cell_60_g), .P(black_cell_60_p));
  Black_Cell black_cell_61 (
    .Gu(black_cell_45_g), .Gl(black_cell_44_g), .Pu(black_cell_45_p), .Pl(black_cell_44_p),
    .G(black_cell_61_g), .P(black_cell_61_p));
  Black_Cell black_cell_62 (
    .Gu(black_cell_46_g), .Gl(black_cell_44_g), .Pu(black_cell_46_p), .Pl(black_cell_44_p),
    .G(black_cell_62_g), .P(black_cell_62_p));
  Black_Cell black_cell_63 (
    .Gu(black_cell_47_g), .Gl(black_cell_44_g), .Pu(black_cell_47_p), .Pl(black_cell_44_p),
    .G(black_cell_63_g), .P(black_cell_63_p));
  Black_Cell black_cell_64 (
    .Gu(black_cell_48_g), .Gl(black_cell_44_g), .Pu(black_cell_48_p), .Pl(black_cell_44_p),
    .G(black_cell_64_g), .P(black_cell_64_p));
  Black_Cell black_cell_65 (
    .Gu(step_1_17_g), .Gl(black_cell_56_g), .Pu(step_1_17_p), .Pl(black_cell_56_p), .G(black_cell_65_g));  // open: P
  Black_Cell black_cell_66 (
    .Gu(black_cell_9_g), .Gl(black_cell_56_g), .Pu(black_cell_9_p), .Pl(black_cell_56_p), .G(black_cell_66_g));  // open: P
  Black_Cell black_cell_67 (
    .Gu(black_cell_25_g), .Gl(black_cell_56_g), .Pu(black_cell_25_p), .Pl(black_cell_56_p),
    .G(black_cell_67_g));  // open: P
  Black_Cell black_cell_68 (
    .Gu(black_cell_26_g), .Gl(black_cell_56_g), .Pu(black_cell_26_p), .Pl(black_cell_56_p),
    .G(black_cell_68_g));  // open: P
  Black_Cell black_cell_69 (
    .Gu(black_cell_41_g), .Gl(black_cell_56_g), .Pu(black_cell_41_p), .Pl(black_cell_56_p),
    .G(black_cell_69_g));  // open: P
  Black_Cell black_cell_70 (
    .Gu(black_cell_42_g), .Gl(black_cell_56_g), .Pu(black_cell_42_p), .Pl(black_cell_56_p),
    .G(black_cell_70_g));  // open: P
  Black_Cell black_cell_71 (
    .Gu(black_cell_43_g), .Gl(black_cell_56_g), .Pu(black_cell_43_p), .Pl(black_cell_56_p),
    .G(black_cell_71_g));  // open: P
  Black_Cell black_cell_72 (
    .Gu(black_cell_44_g), .Gl(black_cell_56_g), .Pu(black_cell_44_p), .Pl(black_cell_56_p),
    .G(black_cell_72_g));  // open: P
  Black_Cell black_cell_73 (
    .Gu(black_cell_57_g), .Gl(black_cell_56_g), .Pu(black_cell_57_p), .Pl(black_cell_56_p),
    .G(black_cell_73_g));  // open: P
  Black_Cell black_cell_74 (
    .Gu(black_cell_58_g), .Gl(black_cell_56_g), .Pu(black_cell_58_p), .Pl(black_cell_56_p),
    .G(black_cell_74_g));  // open: P
  Black_Cell black_cell_75 (
    .Gu(black_cell_59_g), .Gl(black_cell_56_g), .Pu(black_cell_59_p), .Pl(black_cell_56_p),
    .G(black_cell_75_g));  // open: P
  Black_Cell black_cell_76 (
    .Gu(black_cell_60_g), .Gl(black_cell_56_g), .Pu(black_cell_60_p), .Pl(black_cell_56_p),
    .G(black_cell_76_g));  // open: P
  Black_Cell black_cell_77 (
    .Gu(black_cell_61_g), .Gl(black_cell_56_g), .Pu(black_cell_61_p), .Pl(black_cell_56_p),
    .G(black_cell_77_g));  // open: P
  Black_Cell black_cell_78 (
    .Gu(black_cell_62_g), .Gl(black_cell_56_g), .Pu(black_cell_62_p), .Pl(black_cell_56_p),
    .G(black_cell_78_g));  // open: P
  Black_Cell black_cell_79 (
    .Gu(black_cell_63_g), .Gl(black_cell_56_g), .Pu(black_cell_63_p), .Pl(black_cell_56_p),
    .G(black_cell_79_g));  // open: P
  Black_Cell black_cell_80 (
    .Gu(black_cell_64_g), .Gl(black_cell_56_g), .Pu(black_cell_64_p), .Pl(black_cell_56_p),
    .G(black_cell_80_g), .P(black_cell_80_p));
  Black_Cell black_cell_81 (
    .Gu(step_1_33_g), .Gl(black_cell_80_g), .Pu(step_1_33_p), .Pl(black_cell_80_p), .G(Cout));  // open: P
  Sum sum_1 (.A(A[0]), .B(B[0]), .G(step_1_1_g), .S(S[0]));
  Sum sum_2 (.A(A[1]), .B(B[1]), .G(black_cell_1_g), .S(S[1]));
  Sum sum_3 (.A(A[2]), .B(B[2]), .G(black_cell_17_g), .S(S[2]));
  Sum sum_4 (.A(A[3]), .B(B[3]), .G(black_cell_18_g), .S(S[3]));
  Sum sum_5 (.A(A[4]), .B(B[4]), .G(black_cell_33_g), .S(S[4]));
  Sum sum_6 (.A(A[5]), .B(B[5]), .G(black_cell_34_g), .S(S[5]));
  Sum sum_7 (.A(A[6]), .B(B[6]), .G(black_cell_35_g), .S(S[6]));
  Sum sum_8 (.A(A[7]), .B(B[7]), .G(black_cell_36_g), .S(S[7]));
  Sum sum_9 (.A(A[8]), .B(B[8]), .G(black_cell_49_g), .S(S[8]));
  Sum sum_10 (.A(A[9]), .B(B[9]), .G(black_cell_50_g), .S(S[9]));
  Sum sum_11 (.A(A[10]), .B(B[10]), .G(black_cell_51_g), .S(S[10]));
  Sum sum_12 (.A(A[11]), .B(B[11]), .G(black_cell_52_g), .S(S[11]));
  Sum sum_13 (.A(A[12]), .B(B[12]), .G(black_cell_53_g), .S(S[12]));
  Sum sum_14 (.A(A[13]), .B(B[13]), .G(black_cell_54_g), .S(S[13]));
  Sum sum_15 (.A(A[14]), .B(B[14]), .G(black_cell_55_g), .S(S[14]));
  Sum sum_16 (.A(A[15]), .B(B[15]), .G(black_cell_56_g), .S(S[15]));
  Sum sum_17 (.A(A[16]), .B(B[16]), .G(black_cell_65_g), .S(S[16]));
  Sum sum_18 (.A(A[17]), .B(B[17]), .G(black_cell_66_g), .S(S[17]));
  Sum sum_19 (.A(A[18]), .B(B[18]), .G(black_cell_67_g), .S(S[18]));
  Sum sum_20 (.A(A[19]), .B(B[19]), .G(black_cell_68_g), .S(S[19]));
  Sum sum_21 (.A(A[20]), .B(B[20]), .G(black_cell_69_g), .S(S[20]));
  Sum sum_22 (.A(A[21]), .B(B[21]), .G(black_cell_70_g), .S(S[21]));
  Sum sum_23 (.A(A[22]), .B(B[22]), .G(black_cell_71_g), .S(S[22]));
  Sum sum_24 (.A(A[23]), .B(B[23]), .G(black_cell_72_g), .S(S[23]));
  Sum sum_25 (.A(A[24]), .B(B[24]), .G(black_cell_73_g), .S(S[24]));
  Sum sum_26 (.A(A[25]), .B(B[25]), .G(black_cell_74_g), .S(S[25]));
  Sum sum_27 (.A(A[26]), .B(B[26]), .G(black_cell_75_g), .S(S[26]));
  Sum sum_28 (.A(A[27]), .B(B[27]), .G(black_cell_76_g), .S(S[27]));
  Sum sum_29 (.A(A[28]), .B(B[28]), .G(black_cell_77_g), .S(S[28]));
  Sum sum_30 (.A(A[29]), .B(B[29]), .G(black_cell_78_g), .S(S[29]));
  Sum sum_31 (.A(A[30]), .B(B[30]), .G(black_cell_79_g), .S(S[30]));
  Sum sum_32 (.A(A[31]), .B(B[31]), .G(black_cell_80_g), .S(S[31]));

  // Other names for the same wires on the sheet: At[31:0] = A; Bt[31:0] = B
endmodule
