// Logisim project CPU_first_iteration.circ as structural Verilog: 1 circuit, main circuit main
module main (
  input  in_1,
  output [23:0] out_2
);

  wire alu_32bit_1_p4, and_1_out, clock_1_out, control_unit_1_p3, control_unit_1_p4, control_unit_1_p5,
       control_unit_1_p6, control_unit_1_p7, control_unit_1_p8, control_unit_1_p9, control_unit_1_p10;
  wire [4:0] multiplexer_4_out, rom_1_data_3, rom_1_data_4;
  wire [5:0] rom_1_data, rom_1_data_2;
  wire [7:0] alu_32bit_1_p5_2, program_counter_1_pc;
  wire [23:0] alu_32bit_1_p5;
  wire [25:16] rom_1_data_5;
  wire [27:0] adder_1_out;
  wire [31:0] adder_2_out, bit_extender_1_out, data_memory_1_rd, multiplexer_1_out, multiplexer_2_out,
       multiplexer_3_out, multiplexer_5_out, multiplexer_6_out, register_file_test_1_rd1,
       register_file_test_1_rd2, shifter_1_out, shifter_2_out;

  Multiplexer #(.width(32)) multiplexer_1 (
    .in0(multiplexer_3_out), .in1({32{1'b0}}), .out(multiplexer_1_out), .sel(in_1));
  Multiplexer #(.width(32)) multiplexer_2 (
    .in0({shifter_1_out[31:28], adder_1_out}), .in1(adder_2_out), .out(multiplexer_2_out), .sel(and_1_out));
  Multiplexer #(.width(32)) multiplexer_3 (
    .in0(multiplexer_2_out), .in1(shifter_1_out), .out(multiplexer_3_out), .sel(control_unit_1_p9));
  // Probe on multiplexer_4_out
  // Probe on rom_1_data_5[20:16]
  // Probe on rom_1_data_5[25:21]
  Program_Counter program_counter_1 (.CLK(clock_1_out), .PCp(multiplexer_1_out), .PC({out_2, program_counter_1_pc}));
  // Probe on {out_2, program_counter_1_pc}
  // Probe on {rom_1_data, rom_1_data_5, rom_1_data_4, rom_1_data_3, rom_1_data_2}
  Adder #(.width(32)) adder_1 (
    .a({out_2, program_counter_1_pc}), .b(32'h1), .out({shifter_1_out[31:28], adder_1_out}));  // open: cin, cout
  // Probe on control_unit_1_p4
  // Probe on multiplexer_6_out
  Clock clock_1 (.out(clock_1_out));
  ROM #(.dataWidth(32)) rom_1 (
    .addr(program_counter_1_pc), .data({rom_1_data, rom_1_data_5, rom_1_data_4, rom_1_data_3, rom_1_data_2}));
  // Probe on {alu_32bit_1_p5_2, alu_32bit_1_p5}
  // Probe on register_file_test_1_rd1
  // Probe on register_file_test_1_rd2
  // Probe on control_unit_1_p3
  // Probe on control_unit_1_p4
  // Probe on control_unit_1_p5
  // Probe on control_unit_1_p6
  // Probe on control_unit_1_p7
  Multiplexer #(.width(5)) multiplexer_4 (
    .in0(rom_1_data_5[20:16]), .in1(rom_1_data_4), .out(multiplexer_4_out), .sel(control_unit_1_p3));
  assign bit_extender_1_out = {{16{rom_1_data_4[4]}}, {rom_1_data_4, rom_1_data_3, rom_1_data_2}};  // Bit_Extender bit_extender_1
  Shifter #(.width(28)) shifter_1 (
    .in({2'b00, rom_1_data_5, rom_1_data_4, rom_1_data_3, rom_1_data_2}), .\dist (5'b00010),
    .out(shifter_1_out[27:0]));
  // Control_Unit control_unit_1: pin names not known; wires that end beside it: rom_1_data, rom_1_data_2, control_unit_1_p3, control_unit_1_p4, control_unit_1_p5, control_unit_1_p6, control_unit_1_p7, control_unit_1_p8, control_unit_1_p9, control_unit_1_p10
  Shifter #(.width(32)) shifter_2 (.in(bit_extender_1_out), .\dist (5'b00010), .out(shifter_2_out));
  Adder #(.width(32)) adder_2 (
    .a(shifter_2_out), .b({shifter_1_out[31:28], adder_1_out}), .out(adder_2_out));  // open: cin, cout
  Register_File_Test register_file_test_1 (
    .CLK(clock_1_out), .WE3(control_unit_1_p4), .A3(multiplexer_4_out), .WD3(multiplexer_6_out),
    .A1(rom_1_data_5[25:21]), .A2(rom_1_data_5[20:16]), .RD1(register_file_test_1_rd1),
    .RD2(register_file_test_1_rd2));
  Multiplexer #(.width(32)) multiplexer_5 (
    .in0(register_file_test_1_rd2), .in1(bit_extender_1_out), .out(multiplexer_5_out), .sel(control_unit_1_p5));
  // ALU_32bit alu_32bit_1: pin names not known; wires that end beside it: control_unit_1_p10, register_file_test_1_rd1, multiplexer_5_out, alu_32bit_1_p4, {alu_32bit_1_p5_2, alu_32bit_1_p5}
  and and_1 (and_1_out, control_unit_1_p8, alu_32bit_1_p4);
  Data_Memory data_memory_1 (
    .A(alu_32bit_1_p5), .WE(control_unit_1_p7), .CLK(clock_1_out), .WD(register_file_test_1_rd2),
    .RD(data_memory_1_rd));
  Multiplexer #(.width(32)) multiplexer_6 (
    .in0({alu_32bit_1_p5_2, alu_32bit_1_p5}), .in1(data_memory_1_rd), .out(multiplexer_6_out),
    .sel(control_unit_1_p6));

  // Notes on the sheet:
  //   contents of rom_1 (hex, n*v repeats v):
  //   20100003 20110005 2119020 2519822 250a024 251a825 211b02a ac120000 2010000a 20110010 2119020 2519822
  //   250a024 251a825 211b02a ac120004 20100011 2011001b 2119020 2519822 250a024 251a825 211b02a ac120008
  //   20100018 20110026 2119020 2519822 250a024 251a825 211b02a ac12000c 2010001f 20110031 2119020 2519822
  //   250a024 251a825 211b02a ac120010 20100026 2011003c 2119020 2519822 250a024 251a825 211b02a ac120014
  //   2010002d 20110047 2119020 2519822 250a024 251a825 211b02a ac120018 20100034 20110052 2119020 2519822
  //   250a024 251a825 211b02a ac12001c 2010003b 2011005d 2119020 2519822 250a024 251a825 211b02a ac120020
  //   20100042 20110068 2119020 2519822 250a024 251a825 211b02a ac120024 20100049 20110073 2119020 2519822
  //   250a024 251a825 211b02a ac120028 20100050 2011007e 2119020 2519822 250a024 251a825 211b02a ac12002c
  //   20100057 20110089 2119020 2519822 250a024 251a825 211b02a ac120030 2010005e 20110094 2119020 2519822
  //   250a024 251a825 211b02a ac120034 20100065 2011009f 2119020 2519822 250a024 251a825 211b02a ac120038
  //   2010006c 201100aa 2119020 2519822 250a024 251a825 211b02a ac12003c 20100073 201100b5 2119020 2519822
  //   250a024 251a825 211b02a ac120040 2010007a 201100c0 2119020 2519822 250a024 251a825 211b02a ac120044
  //   20100081 201100cb 2119020 2519822 250a024 251a825 211b02a ac120048 20100088 201100d6 2119020 2519822
  //   250a024 251a825 211b02a ac12004c 2010008f 201100e1 2119020 2519822 250a024 251a825 211b02a ac120050
  //   20100096 201100ec 2119020 2519822 250a024 251a825 211b02a ac120054 2010009d 201100f7 2119020 2519822
  //   250a024 251a825 211b02a ac120058 201000a4 20110102 2119020 2519822 250a024 251a825 211b02a ac12005c
  //   201000ab 2011010d 2119020 2519822 250a024 251a825 211b02a ac120060
endmodule
