// Logisim project Control_Unit.circ as structural Verilog: 2 circuits, main circuit Control_Unit
module Control_Unit (
  input  [5:0] Opcode,
  input  [5:0] Funct,
  output RegDst,
  output RegWrite,
  output ALUSrc,
  output MemtoReg,
  output MemWrite,
  output Branch,
  output Jump,
  output [2:0] ALUControl
);

  wire and_3_out, and_4_out, nor_3_out, nor_5_out, nor_6_out, not_1_out, not_2_out, not_3_out, not_4_out,
       not_5_out, not_6_out, not_7_out, not_8_out, not_9_out, not_10_out, not_11_out, not_12_out, not_13_out,
       not_14_out, not_15_out, not_16_out, not_17_out;
  wire [2:0] or_3_out;

  not not_1 (not_1_out, Opcode[2]);
  not not_2 (not_2_out, Opcode[3]);
  not not_3 (not_3_out, Opcode[4]);
  not not_4 (not_4_out, Opcode[2]);
  not not_5 (not_5_out, Opcode[4]);
  not not_6 (not_6_out, Opcode[2]);
  not not_7 (not_7_out, Opcode[3]);
  not not_8 (not_8_out, Opcode[1]);
  nor nor_1 (RegDst, Opcode[2], Opcode[0], Opcode[1], Opcode[3], Opcode[4], Opcode[5]);
  and and_1 (MemtoReg, Opcode[0], Opcode[1], not_1_out, not_2_out, not_3_out, Opcode[5]);
  and and_2 (MemWrite, Opcode[0], Opcode[1], not_4_out, Opcode[3], not_5_out, Opcode[5]);
  nor nor_2 (Branch, Opcode[0], Opcode[1], not_6_out, Opcode[3], Opcode[4], Opcode[5]);
  nor nor_3 (nor_3_out, Opcode[0], Opcode[1], Opcode[2], not_7_out, Opcode[4], Opcode[5]);
  nor nor_4 (Jump, Opcode[0], not_8_out, Opcode[2], Opcode[3], Opcode[4], Opcode[5]);
  or or_1 (RegWrite, RegDst, MemtoReg, nor_3_out);
  or or_2 (ALUSrc, MemtoReg, MemWrite, nor_3_out);
  not not_9 (not_9_out, Funct[0]);
  not not_10 (not_10_out, Funct[5]);
  not not_11 (not_11_out, Funct[1]);
  not not_12 (not_12_out, Funct[5]);
  not not_13 (not_13_out, Funct[1]);
  and and_3 (and_3_out, Funct[0], Funct[2], not_13_out, not_14_out, not_15_out, Funct[5]);
  not not_14 (not_14_out, Funct[3]);
  not not_15 (not_15_out, Funct[4]);
  not not_16 (not_16_out, Funct[2]);
  and and_4 (and_4_out, not_9_out, Funct[1], not_16_out, Funct[3], not_17_out, Funct[5]);
  not not_17 (not_17_out, Funct[4]);
  nor nor_5 (nor_5_out, Funct[0], Funct[1], Funct[2], Funct[3], Funct[4], not_10_out);
  nor nor_6 (nor_6_out, Funct[0], not_11_out, Funct[2], Funct[3], Funct[4], not_12_out);
  or or_3 (or_3_out[0], and_3_out, and_4_out);
  or or_4 (or_3_out[1], nor_5_out, nor_6_out, and_4_out);
  or or_5 (or_3_out[2], nor_6_out, and_4_out);
  Multiplexer #(.select(2), .width(3)) multiplexer_1 (
    .in0(3'b010), .in1(3'b110), .in2(or_3_out), .in3(or_3_out), .out(ALUControl), .sel({RegDst, Branch}));
endmodule

module Control_Unit_Extended (
  input  [5:0] Opcode,
  input  [5:0] Funct,
  output RegDst,
  output ALUSrc,
  output ImmExtend,
  output JumpReg,
  output Shift,
  output MemtoReg,
  output MemWrite,
  output Branch,
  output BranchNot,
  output Jump,
  output JumpandLink,
  output RegWrite,
  output [4:0] ALUControl
);

  wire and_1_out, nor_2_out, nor_3_out, nor_4_out, nor_5_out, nor_8_out, nor_10_out, nor_11_out, nor_12_out,
       nor_14_out, nor_15_out, nor_16_out, nor_20_out, nor_21_out, not_1_out, not_2_out, not_3_out,
       not_4_out, not_5_out, not_6_out, not_7_out, not_8_out, not_9_out, not_10_out, not_11_out, not_12_out,
       not_13_out, not_14_out, not_15_out, not_16_out, not_17_out, not_18_out, not_19_out, not_20_out,
       not_21_out, not_22_out, not_23_out, not_24_out, not_25_out, not_26_out, not_27_out, not_28_out,
       not_29_out, not_30_out, not_31_out, not_32_out, not_33_out, not_34_out, not_35_out, not_36_out,
       not_37_out, not_38_out, not_39_out, not_40_out, not_41_out, not_42_out, not_43_out, not_44_out,
       not_45_out, not_46_out, not_47_out, or_7_out, or_12_out;
  wire [1:0] nor_17_out;
  wire [2:0] or_3_out;
  wire [4:0] or_11_out;

  not not_1 (not_1_out, Opcode[3]);
  not not_2 (not_2_out, Opcode[2]);
  not not_3 (not_3_out, Opcode[3]);
  not not_4 (not_4_out, Opcode[0]);
  not not_5 (not_5_out, Opcode[2]);
  not not_6 (not_6_out, Opcode[3]);
  not not_7 (not_7_out, Opcode[4]);
  not not_8 (not_8_out, Opcode[5]);
  not not_9 (not_9_out, Opcode[1]);
  not not_10 (not_10_out, Opcode[3]);
  not not_11 (not_11_out, Opcode[2]);
  not not_12 (not_12_out, Opcode[3]);
  not not_13 (not_13_out, Opcode[4]);
  not not_14 (not_14_out, Opcode[2]);
  not not_15 (not_15_out, Opcode[4]);
  not not_16 (not_16_out, Opcode[2]);
  not not_17 (not_17_out, Opcode[0]);
  not not_18 (not_18_out, Opcode[2]);
  not not_19 (not_19_out, Opcode[1]);
  not not_20 (not_20_out, Opcode[0]);
  not not_21 (not_21_out, Opcode[1]);
  not not_22 (not_22_out, Opcode[1]);
  not not_23 (not_23_out, Opcode[2]);
  not not_24 (not_24_out, Opcode[3]);
  nor nor_1 (RegDst, Opcode[0], Opcode[1], Opcode[2], Opcode[3], Opcode[4], Opcode[5]);
  nor nor_2 (nor_2_out, Opcode[0], Opcode[1], Opcode[2], not_1_out, Opcode[4], Opcode[5]);
  nor nor_3 (nor_3_out, Opcode[0], Opcode[1], not_2_out, not_3_out, Opcode[4], Opcode[5]);
  nor nor_4 (nor_4_out, not_4_out, Opcode[1], not_5_out, not_6_out, Opcode[4], Opcode[5]);
  and and_1 (and_1_out, Opcode[0], Opcode[1], Opcode[2], Opcode[3], not_7_out, not_8_out);
  nor nor_5 (nor_5_out, Opcode[0], not_9_out, Opcode[2], not_10_out, Opcode[4], Opcode[5]);
  and and_2 (MemtoReg, Opcode[0], Opcode[1], not_11_out, not_12_out, not_13_out, Opcode[5]);
  and and_3 (MemWrite, Opcode[0], Opcode[1], not_14_out, Opcode[3], not_15_out, Opcode[5]);
  nor nor_6 (Branch, Opcode[0], Opcode[1], not_16_out, Opcode[3], Opcode[4], Opcode[5]);
  nor nor_7 (BranchNot, not_17_out, Opcode[1], not_18_out, Opcode[3], Opcode[4], Opcode[5]);
  nor nor_8 (nor_8_out, Opcode[0], not_19_out, Opcode[2], Opcode[3], Opcode[4], Opcode[5]);
  nor nor_9 (JumpandLink, not_20_out, not_21_out, Opcode[2], Opcode[3], Opcode[4], Opcode[5]);
  nor nor_10 (nor_10_out, Opcode[0], not_22_out, not_23_out, not_24_out, Opcode[4], Opcode[5]);
  not not_25 (not_25_out, Funct[5]);
  not not_26 (not_26_out, Funct[1]);
  not not_27 (not_27_out, Funct[5]);
  not not_28 (not_28_out, Funct[2]);
  not not_29 (not_29_out, Funct[5]);
  not not_30 (not_30_out, Funct[0]);
  not not_31 (not_31_out, Funct[2]);
  not not_32 (not_32_out, Funct[5]);
  not not_33 (not_33_out, Funct[1]);
  not not_34 (not_34_out, Funct[3]);
  not not_35 (not_35_out, Funct[5]);
  not not_36 (not_36_out, Funct[3]);
  not not_37 (not_37_out, Funct[1]);
  not not_38 (not_38_out, Funct[0]);
  not not_39 (not_39_out, Funct[1]);
  not not_40 (not_40_out, Funct[0]);
  not not_41 (not_41_out, Funct[1]);
  not not_42 (not_42_out, Funct[2]);
  not not_43 (not_43_out, Funct[5]);
  not not_44 (not_44_out, Funct[1]);
  not not_45 (not_45_out, Funct[2]);
  not not_46 (not_46_out, Funct[5]);
  nor nor_11 (nor_11_out, Funct[0], Funct[1], Funct[2], Funct[3], Funct[4], not_25_out);
  nor nor_12 (nor_12_out, Funct[0], not_26_out, Funct[2], Funct[3], Funct[4], not_27_out);
  // NOR_Gate nor_13 has open pins: in0=Funct[0], in1=Funct[1], in2=not_28_out, in3=Funct[3], in4=Funct[4], in5=not_29_out, out=open
  nor nor_14 (nor_14_out, not_30_out, Funct[1], not_31_out, Funct[3], Funct[4], not_32_out);
  nor nor_15 (nor_15_out, Funct[0], not_33_out, Funct[2], not_34_out, Funct[4], not_35_out);
  nor nor_16 (nor_16_out, Funct[0], Funct[1], Funct[2], not_36_out, Funct[4], Funct[5]);
  nor nor_17 (nor_17_out[0], Funct[0], Funct[1], Funct[2], Funct[3], Funct[4], Funct[5]);
  nor nor_18 (nor_17_out[1], Funct[0], not_37_out, Funct[2], Funct[3], Funct[4], Funct[5]);
  nor nor_19 (or_11_out[3], not_38_out, not_39_out, Funct[2], Funct[3], Funct[4], Funct[5]);
  nor nor_20 (nor_20_out, not_40_out, not_41_out, not_42_out, Funct[3], Funct[4], not_43_out);
  nor nor_21 (nor_21_out, Funct[0], not_44_out, not_45_out, Funct[3], Funct[4], not_46_out);
  or or_1 (or_3_out[2], RegDst, and_1_out, nor_5_out, nor_10_out);
  or or_2 (or_3_out[1], RegDst, nor_3_out, nor_4_out, nor_10_out);
  or or_3 (or_3_out[0], RegDst, nor_5_out, nor_4_out, BranchNot, Branch);
  or or_4 (ALUSrc, nor_2_out, nor_3_out, nor_4_out, and_1_out, nor_5_out, MemtoReg, MemWrite, nor_10_out);
  or or_5 (ImmExtend, nor_3_out, nor_4_out, and_1_out, nor_10_out);
  or or_6 (Jump, nor_8_out, JumpandLink);
  or or_7 (or_7_out, RegDst, nor_2_out, nor_3_out, nor_4_out, and_1_out, nor_5_out, MemtoReg, JumpandLink, nor_10_out);
  or or_8 (or_11_out[4], nor_12_out, nor_15_out);
  or or_9 (or_11_out[2], nor_17_out[0], nor_17_out[1], nor_20_out, nor_21_out);
  or or_10 (or_11_out[1], nor_11_out, nor_12_out, nor_15_out, nor_16_out, nor_17_out[0], nor_17_out[1]);
  or or_11 (or_11_out[0], nor_14_out, nor_15_out, nor_17_out[1], nor_20_out);
  or or_12 (or_12_out, nor_17_out[0], nor_17_out[1], or_11_out[3]);
  not not_47 (not_47_out, JumpReg);
  and and_4 (JumpReg, RegDst, nor_16_out);
  and and_5 (Shift, RegDst, or_12_out);
  and and_6 (RegWrite, not_47_out, or_7_out);
  Multiplexer #(.select(3), .width(5)) multiplexer_1 (
    .in0(5'b00010), .in1(5'b10010), .in2({5{1'b0}}), .in3(5'b00001), .in4(5'b01001), .in5(5'b10011),
    .in6(5'b00100), .in7(or_11_out), .out(ALUControl), .sel(or_3_out));

  // Notes on the sheet:
  //   R-type
  //   addi
  //   andi
  //   ori
  //   lui
  //   slti
  //   lw
  //   sw
  //   beq
  //   bne
  //   j
  //   jal
  //   xori
  //   add
  //   sub
  //   and
  //   or
  //   slt
  //   jr
  //   sll
  //   srl
  //   sra
  //   nor
  //   xor
endmodule
