// Logisim project Data_Memory.circ as structural Verilog: 1 circuit, main circuit Data_Memory
module Data_Memory (
  input  [23:0] A,
  input  WE,
  input  CLK,
  input  [31:0] WD,
  output [31:0] RD
);

  wire not_1_out;

  RAM #(.addrWidth(24), .dataWidth(32), .enables("line")) ram_1 (
    .addr(A), .we(WE), .oe(not_1_out), .clk(CLK), .din(WD), .dout(RD));
  not not_1 (not_1_out, WE);
endmodule
