// Logisim project Program_Counter.circ as structural Verilog: 1 circuit, main circuit Program_Counter
module Program_Counter (
  input  CLK,
  input  [31:0] PCp,
  output [31:0] PC
);

  D_flip_flop d_flip_flop_1 (.CLK(CLK), .D(PCp[31]), .Q(PC[31]));  // open: Qp
  D_flip_flop d_flip_flop_2 (.CLK(CLK), .D(PCp[30]), .Q(PC[30]));  // open: Qp
  D_flip_flop d_flip_flop_3 (.CLK(CLK), .D(PCp[29]), .Q(PC[29]));  // open: Qp
  D_flip_flop d_flip_flop_4 (.CLK(CLK), .D(PCp[28]), .Q(PC[28]));  // open: Qp
  D_flip_flop d_flip_flop_5 (.CLK(CLK), .D(PCp[27]), .Q(PC[27]));  // open: Qp
  D_flip_flop d_flip_flop_6 (.CLK(CLK), .D(PCp[26]), .Q(PC[26]));  // open: Qp
  D_flip_flop d_flip_flop_7 (.CLK(CLK), .D(PCp[25]), .Q(PC[25]));  // open: Qp
  D_flip_flop d_flip_flop_8 (.CLK(CLK), .D(PCp[24]), .Q(PC[24]));  // open: Qp
  D_flip_flop d_flip_flop_9 (.CLK(CLK), .D(PCp[23]), .Q(PC[23]));  // open: Qp
  D_flip_flop d_flip_flop_10 (.CLK(CLK), .D(PCp[22]), .Q(PC[22]));  // open: Qp
  D_flip_flop d_flip_flop_11 (.CLK(CLK), .D(PCp[21]), .Q(PC[21]));  // open: Qp
  D_flip_flop d_flip_flop_12 (.CLK(CLK), .D(PCp[20]), .Q(PC[20]));  // open: Qp
  D_flip_flop d_flip_flop_13 (.CLK(CLK), .D(PCp[19]), .Q(PC[19]));  // open: Qp
  D_flip_flop d_flip_flop_14 (.CLK(CLK), .D(PCp[18]), .Q(PC[18]));  // open: Qp
  D_flip_flop d_flip_flop_15 (.CLK(CLK), .D(PCp[17]), .Q(PC[17]));  // open: Qp
  D_flip_flop d_flip_flop_16 (.CLK(CLK), .D(PCp[16]), .Q(PC[16]));  // open: Qp
  D_flip_flop d_flip_flop_17 (.CLK(CLK), .D(PCp[15]), .Q(PC[15]));  // open: Qp
  D_flip_flop d_flip_flop_18 (.CLK(CLK), .D(PCp[14]), .Q(PC[14]));  // open: Qp
  D_flip_flop d_flip_flop_19 (.CLK(CLK), .D(PCp[13]), .Q(PC[13]));  // open: Qp
  D_flip_flop d_flip_flop_20 (.CLK(CLK), .D(PCp[12]), .Q(PC[12]));  // open: Qp
  D_flip_flop d_flip_flop_21 (.CLK(CLK), .D(PCp[11]), .Q(PC[11]));  // open: Qp
  D_flip_flop d_flip_flop_22 (.CLK(CLK), .D(PCp[10]), .Q(PC[10]));  // open: Qp
  D_flip_flop d_flip_flop_23 (.CLK(CLK), .D(PCp[9]), .Q(PC[9]));  // open: Qp
  D_flip_flop d_flip_flop_24 (.CLK(CLK), .D(PCp[8]), .Q(PC[8]));  // open: Qp
  D_flip_flop d_flip_flop_25 (.CLK(CLK), .D(PCp[7]), .Q(PC[7]));  // open: Qp
  D_flip_flop d_flip_flop_26 (.CLK(CLK), .D(PCp[6]), .Q(PC[6]));  // open: Qp
  D_flip_flop d_flip_flop_27 (.CLK(CLK), .D(PCp[5]), .Q(PC[5]));  // open: Qp
  D_flip_flop d_flip_flop_28 (.CLK(CLK), .D(PCp[4]), .Q(PC[4]));  // open: Qp
  D_flip_flop d_flip_flop_29 (.CLK(CLK), .D(PCp[3]), .Q(PC[3]));  // open: Qp
  D_flip_flop d_flip_flop_30 (.CLK(CLK), .D(PCp[2]), .Q(PC[2]));  // open: Qp
  D_flip_flop d_flip_flop_31 (.CLK(CLK), .D(PCp[1]), .Q(PC[1]));  // open: Qp
  D_flip_flop d_flip_flop_32 (.CLK(CLK), .D(PCp[0]), .Q(PC[0]));  // open: Qp
endmodule
