// Logisim project Register_file.circ as structural Verilog: 2 circuits, main circuit Register_32bit
module Register_32bit (
  input  CLK,
  input  [31:0] Reg_In,
  output [31:0] Reg_Out
);

  D_flip_flop d_flip_flop_1 (.CLK(CLK), .D(Reg_In[3]), .Q(Reg_Out[3]));  // open: Qp
  D_flip_flop d_flip_flop_2 (.CLK(CLK), .D(Reg_In[2]), .Q(Reg_Out[2]));  // open: Qp
  D_flip_flop d_flip_flop_3 (.CLK(CLK), .D(Reg_In[1]), .Q(Reg_Out[1]));  // open: Qp
  D_flip_flop d_flip_flop_4 (.CLK(CLK), .D(Reg_In[0]), .Q(Reg_Out[0]));  // open: Qp
  D_flip_flop d_flip_flop_5 (.CLK(CLK), .D(Reg_In[7]), .Q(Reg_Out[7]));  // open: Qp
  D_flip_flop d_flip_flop_6 (.CLK(CLK), .D(Reg_In[6]), .Q(Reg_Out[6]));  // open: Qp
  D_flip_flop d_flip_flop_7 (.CLK(CLK), .D(Reg_In[5]), .Q(Reg_Out[5]));  // open: Qp
  D_flip_flop d_flip_flop_8 (.CLK(CLK), .D(Reg_In[4]), .Q(Reg_Out[4]));  // open: Qp
  D_flip_flop d_flip_flop_9 (.CLK(CLK), .D(Reg_In[11]), .Q(Reg_Out[11]));  // open: Qp
  D_flip_flop d_flip_flop_10 (.CLK(CLK), .D(Reg_In[10]), .Q(Reg_Out[10]));  // open: Qp
  D_flip_flop d_flip_flop_11 (.CLK(CLK), .D(Reg_In[9]), .Q(Reg_Out[9]));  // open: Qp
  D_flip_flop d_flip_flop_12 (.CLK(CLK), .D(Reg_In[8]), .Q(Reg_Out[8]));  // open: Qp
  D_flip_flop d_flip_flop_13 (.CLK(CLK), .D(Reg_In[15]), .Q(Reg_Out[15]));  // open: Qp
  D_flip_flop d_flip_flop_14 (.CLK(CLK), .D(Reg_In[14]), .Q(Reg_Out[14]));  // open: Qp
  D_flip_flop d_flip_flop_15 (.CLK(CLK), .D(Reg_In[13]), .Q(Reg_Out[13]));  // open: Qp
  D_flip_flop d_flip_flop_16 (.CLK(CLK), .D(Reg_In[12]), .Q(Reg_Out[12]));  // open: Qp
  D_flip_flop d_flip_flop_17 (.CLK(CLK), .D(Reg_In[19]), .Q(Reg_Out[19]));  // open: Qp
  D_flip_flop d_flip_flop_18 (.CLK(CLK), .D(Reg_In[18]), .Q(Reg_Out[18]));  // open: Qp
  D_flip_flop d_flip_flop_19 (.CLK(CLK), .D(Reg_In[17]), .Q(Reg_Out[17]));  // open: Qp
  D_flip_flop d_flip_flop_20 (.CLK(CLK), .D(Reg_In[16]), .Q(Reg_Out[16]));  // open: Qp
  D_flip_flop d_flip_flop_21 (.CLK(CLK), .D(Reg_In[23]), .Q(Reg_Out[23]));  // open: Qp
  D_flip_flop d_flip_flop_22 (.CLK(CLK), .D(Reg_In[22]), .Q(Reg_Out[22]));  // open: Qp
  D_flip_flop d_flip_flop_23 (.CLK(CLK), .D(Reg_In[21]), .Q(Reg_Out[21]));  // open: Qp
  D_flip_flop d_flip_flop_24 (.CLK(CLK), .D(Reg_In[20]), .Q(Reg_Out[20]));  // open: Qp
  D_flip_flop d_flip_flop_25 (.CLK(CLK), .D(Reg_In[27]), .Q(Reg_Out[27]));  // open: Qp
  D_flip_flop d_flip_flop_26 (.CLK(CLK), .D(Reg_In[26]), .Q(Reg_Out[26]));  // open: Qp
  D_flip_flop d_flip_flop_27 (.CLK(CLK), .D(Reg_In[25]), .Q(Reg_Out[25]));  // open: Qp
  D_flip_flop d_flip_flop_28 (.CLK(CLK), .D(Reg_In[24]), .Q(Reg_Out[24]));  // open: Qp
  D_flip_flop d_flip_flop_29 (.CLK(CLK), .D(Reg_In[31]), .Q(Reg_Out[31]));  // open: Qp
  D_flip_flop d_flip_flop_30 (.CLK(CLK), .D(Reg_In[30]), .Q(Reg_Out[30]));  // open: Qp
  D_flip_flop d_flip_flop_31 (.CLK(CLK), .D(Reg_In[29]), .Q(Reg_Out[29]));  // open: Qp
  D_flip_flop d_flip_flop_32 (.CLK(CLK), .D(Reg_In[28]), .Q(Reg_Out[28]));  // open: Qp
endmodule

module Register_File_Test (
  input  CLK,
  input  WE3,
  input  [4:0] A3,
  input  [31:0] WD3,
  input  [4:0] A1,
  input  [4:0] A2,
  output [31:0] RD1,
  output [31:0] RD2
);

  wire decoder_1_out1, decoder_1_out2, decoder_1_out3, decoder_1_out4, decoder_1_out5, decoder_1_out6,
       decoder_1_out7, decoder_1_out8, decoder_1_out9, decoder_1_out10, decoder_1_out11, decoder_1_out12,
       decoder_1_out13, decoder_1_out14, decoder_1_out15;
  wire [15:0] decoder_1_out16;
  wire [31:0] register_1_q, register_2_q, register_3_q, register_4_q, register_5_q, register_6_q,
       register_7_q, register_8_q, register_9_q, register_10_q, register_11_q, register_12_q, register_13_q,
       register_14_q, register_15_q, register_16_q, register_17_q, register_18_q, register_19_q,
       register_20_q, register_21_q, register_22_q, register_23_q, register_24_q, register_25_q,
       register_26_q, register_27_q, register_28_q, register_29_q, register_30_q, register_31_q;

  Decoder #(.select(5)) decoder_1 (
    .out1(decoder_1_out1), .out2(decoder_1_out2), .out3(decoder_1_out3), .out4(decoder_1_out4),
    .out5(decoder_1_out5), .out6(decoder_1_out6), .out7(decoder_1_out7), .out8(decoder_1_out8),
    .out9(decoder_1_out9), .out10(decoder_1_out10), .out11(decoder_1_out11), .out12(decoder_1_out12),
    .out13(decoder_1_out13), .out14(decoder_1_out14), .out15(decoder_1_out15), .out16(decoder_1_out16[0]),
    .out17(decoder_1_out16[1]), .out18(decoder_1_out16[2]), .out19(decoder_1_out16[3]),
    .out20(decoder_1_out16[4]), .out21(decoder_1_out16[5]), .out22(decoder_1_out16[6]),
    .out23(decoder_1_out16[7]), .out24(decoder_1_out16[8]), .out25(decoder_1_out16[9]),
    .out26(decoder_1_out16[10]), .out27(decoder_1_out16[11]), .out28(decoder_1_out16[12]),
    .out29(decoder_1_out16[13]), .out30(decoder_1_out16[14]), .out31(decoder_1_out16[15]), .sel(A3), .en(WE3));  // open: out0
  Register #(.width(32)) register_1 (.D(WD3), .en(decoder_1_out1), .clk(CLK), .Q(register_1_q));  // open: clr
  Register #(.width(32)) register_2 (.D(WD3), .en(decoder_1_out2), .clk(CLK), .Q(register_2_q));  // open: clr
  Register #(.width(32)) register_3 (.D(WD3), .en(decoder_1_out3), .clk(CLK), .Q(register_3_q));  // open: clr
  Register #(.width(32)) register_4 (.D(WD3), .en(decoder_1_out4), .clk(CLK), .Q(register_4_q));  // open: clr
  Register #(.width(32)) register_5 (.D(WD3), .en(decoder_1_out5), .clk(CLK), .Q(register_5_q));  // open: clr
  Register #(.width(32)) register_6 (.D(WD3), .en(decoder_1_out6), .clk(CLK), .Q(register_6_q));  // open: clr
  Register #(.width(32)) register_7 (.D(WD3), .en(decoder_1_out7), .clk(CLK), .Q(register_7_q));  // open: clr
  Register #(.width(32)) register_8 (.D(WD3), .en(decoder_1_out8), .clk(CLK), .Q(register_8_q));  // open: clr
  Register #(.width(32)) register_9 (.D(WD3), .en(decoder_1_out9), .clk(CLK), .Q(register_9_q));  // open: clr
  Register #(.width(32)) register_10 (.D(WD3), .en(decoder_1_out10), .clk(CLK), .Q(register_10_q));  // open: clr
  Register #(.width(32)) register_11 (.D(WD3), .en(decoder_1_out11), .clk(CLK), .Q(register_11_q));  // open: clr
  Register #(.width(32)) register_12 (.D(WD3), .en(decoder_1_out12), .clk(CLK), .Q(register_12_q));  // open: clr
  Register #(.width(32)) register_13 (.D(WD3), .en(decoder_1_out13), .clk(CLK), .Q(register_13_q));  // open: clr
  Register #(.width(32)) register_14 (.D(WD3), .en(decoder_1_out14), .clk(CLK), .Q(register_14_q));  // open: clr
  Register #(.width(32)) register_15 (.D(WD3), .en(decoder_1_out15), .clk(CLK), .Q(register_15_q));  // open: clr
  Register #(.width(32)) register_16 (.D(WD3), .en(decoder_1_out16[0]), .clk(CLK), .Q(register_16_q));  // open: clr
  Register #(.width(32)) register_17 (.D(WD3), .en(decoder_1_out16[1]), .clk(CLK), .Q(register_17_q));  // open: clr
  Register #(.width(32)) register_18 (.D(WD3), .en(decoder_1_out16[2]), .clk(CLK), .Q(register_18_q));  // open: clr
  Register #(.width(32)) register_19 (.D(WD3), .en(decoder_1_out16[3]), .clk(CLK), .Q(register_19_q));  // open: clr
  Register #(.width(32)) register_20 (.D(WD3), .en(decoder_1_out16[4]), .clk(CLK), .Q(register_20_q));  // open: clr
  Register #(.width(32)) register_21 (.D(WD3), .en(decoder_1_out16[5]), .clk(CLK), .Q(register_21_q));  // open: clr
  Register #(.width(32)) register_22 (.D(WD3), .en(decoder_1_out16[6]), .clk(CLK), .Q(register_22_q));  // open: clr
  Register #(.width(32)) register_23 (.D(WD3), .en(decoder_1_out16[7]), .clk(CLK), .Q(register_23_q));  // open: clr
  Register #(.width(32)) register_24 (.D(WD3), .en(decoder_1_out16[8]), .clk(CLK), .Q(register_24_q));  // open: clr
  Register #(.width(32)) register_25 (.D(WD3), .en(decoder_1_out16[9]), .clk(CLK), .Q(register_25_q));  // open: clr
  Register #(.width(32)) register_26 (.D(WD3), .en(decoder_1_out16[10]), .clk(CLK), .Q(register_26_q));  // open: clr
  Register #(.width(32)) register_27 (.D(WD3), .en(decoder_1_out16[11]), .clk(CLK), .Q(register_27_q));  // open: clr
  Register #(.width(32)) register_28 (.D(WD3), .en(decoder_1_out16[12]), .clk(CLK), .Q(register_28_q));  // open: clr
  Register #(.width(32)) register_29 (.D(WD3), .en(decoder_1_out16[13]), .clk(CLK), .Q(register_29_q));  // open: clr
  Register #(.width(32)) register_30 (.D(WD3), .en(decoder_1_out16[14]), .clk(CLK), .Q(register_30_q));  // open: clr
  Register #(.width(32)) register_31 (.D(WD3), .en(decoder_1_out16[15]), .clk(CLK), .Q(register_31_q));  // open: clr
  // Probe on register_16_q
  // Probe on register_17_q
  // Probe on register_18_q
  // Probe on register_19_q
  // Probe on register_20_q
  // Probe on register_21_q
  // Probe on register_22_q
  // Probe on register_23_q
  Multiplexer #(.select(5), .width(32)) multiplexer_1 (
    .in0({32{1'b0}}), .in1(register_1_q), .in2(register_2_q), .in3(register_3_q), .in4(register_4_q),
    .in5(register_5_q), .in6(register_6_q), .in7(register_7_q), .in8(register_8_q), .in9(register_9_q),
    .in10(register_10_q), .in11(register_11_q), .in12(register_12_q), .in13(register_13_q),
    .in14(register_14_q), .in15(register_15_q), .in16(register_16_q), .in17(register_17_q),
    .in18(register_18_q), .in19(register_19_q), .in20(register_20_q), .in21(register_21_q),
    .in22(register_22_q), .in23(register_23_q), .in24(register_24_q), .in25(register_25_q),
    .in26(register_26_q), .in27(register_27_q), .in28(register_28_q), .in29(register_29_q),
    .in30(register_30_q), .in31(register_31_q), .out(RD1), .sel(A1));
  Multiplexer #(.select(5), .width(32)) multiplexer_2 (
    .in0({32{1'b0}}), .in1(register_1_q), .in2(register_2_q), .in3(register_3_q), .in4(register_4_q),
    .in5(register_5_q), .in6(register_6_q), .in7(register_7_q), .in8(register_8_q), .in9(register_9_q),
    .in10(register_10_q), .in11(register_11_q), .in12(register_12_q), .in13(register_13_q),
    .in14(register_14_q), .in15(register_15_q), .in16(register_16_q), .in17(register_17_q),
    .in18(register_18_q), .in19(register_19_q), .in20(register_20_q), .in21(register_21_q),
    .in22(register_22_q), .in23(register_23_q), .in24(register_24_q), .in25(register_25_q),
    .in26(register_26_q), .in27(register_27_q), .in28(register_28_q), .in29(register_29_q),
    .in30(register_30_q), .in31(register_31_q), .out(RD2), .sel(A2));
endmodule
