// Logisim project building_blocks.circ as structural Verilog: 2 circuits, main circuit D_latch
module D_latch (
  input  CLK,
  input  D,
  output Q,
  output Qp
);

  wire and_1_out, and_2_out, not_1_out;

  not not_1 (not_1_out, D);
  and and_1 (and_1_out, CLK, not_1_out);
  and and_2 (and_2_out, CLK, D);
  nor nor_1 (Q, and_1_out, Qp);
  nor nor_2 (Qp, Q, and_2_out);
endmodule

module D_flip_flop (
  input  CLK,
  input  D,
  output Q,
  output Qp
);

  wire d_latch_1_q, not_1_out;

  not not_1 (not_1_out, CLK);
  D_latch d_latch_1 (.CLK(not_1_out), .D(D), .Q(d_latch_1_q));  // open: Qp
  D_latch d_latch_2 (.CLK(CLK), .D(d_latch_1_q), .Q(Q), .Qp(Qp));
endmodule
