// Logisim project complete_single_cycle.circ as structural Verilog: 2 circuits, main circuit main
module main (
  input  in_1
);

  wire alu_32bit_1_zero, and_1_out, and_2_out, clock_1_out, control_unit_extended_1_alusrc,
       control_unit_extended_1_branch, control_unit_extended_1_branchnot, control_unit_extended_1_immextend,
       control_unit_extended_1_jump, control_unit_extended_1_jumpandlink, control_unit_extended_1_jumpreg,
       control_unit_extended_1_memtoreg, control_unit_extended_1_memwrite, control_unit_extended_1_regdst,
       control_unit_extended_1_regwrite, control_unit_extended_1_shift, not_1_out;
  wire [1:0] program_counter_1_pc;
  wire [4:0] control_unit_extended_1_alucontrol, multiplexer_8_out, multiplexer_9_out;
  wire [5:0] program_counter_1_pc_3;
  wire [23:0] program_counter_1_pc_2;
  wire [27:0] adder_1_out;
  wire [31:0] adder_2_out, alu_32bit_1_aluresult, bit_extender_1_out, bit_extender_2_out, bit_extender_3_out,
       data_memory_1_rd, multiplexer_1_out, multiplexer_2_out, multiplexer_3_out, multiplexer_4_out,
       multiplexer_5_out, multiplexer_6_out, multiplexer_7_out, multiplexer_10_out, multiplexer_11_out,
       multiplexer_12_out, register_file_test_1_rd1, register_file_test_1_rd2, rom_1_data, shifter_1_out,
       shifter_2_out;

  Multiplexer #(.width(32)) multiplexer_1 (
    .in0(multiplexer_5_out), .in1({32{1'b0}}), .out(multiplexer_1_out), .sel(in_1));
  Multiplexer #(.width(32)) multiplexer_2 (
    .in0({shifter_1_out[31:28], adder_1_out}), .in1(adder_2_out), .out(multiplexer_2_out), .sel(and_2_out));
  Multiplexer #(.width(32)) multiplexer_3 (
    .in0(multiplexer_2_out), .in1(adder_2_out), .out(multiplexer_3_out), .sel(and_1_out));
  Multiplexer #(.width(32)) multiplexer_4 (
    .in0(multiplexer_3_out), .in1(shifter_1_out), .out(multiplexer_4_out), .sel(control_unit_extended_1_jump));
  Multiplexer #(.width(32)) multiplexer_5 (
    .in0(multiplexer_4_out), .in1(register_file_test_1_rd1), .out(multiplexer_5_out),
    .sel(control_unit_extended_1_jumpreg));
  Clock clock_1 (.out(clock_1_out));
  Adder #(.width(32)) adder_1 (
    .a({program_counter_1_pc_3, program_counter_1_pc_2, program_counter_1_pc}), .b(32'h4),
    .out({shifter_1_out[31:28], adder_1_out}));  // open: cin, cout
  // Probe on {program_counter_1_pc_3, program_counter_1_pc_2, program_counter_1_pc}
  Program_Counter program_counter_1 (
    .CLK(clock_1_out), .PCp(multiplexer_1_out),
    .PC({program_counter_1_pc_3, program_counter_1_pc_2, program_counter_1_pc}));
  ROM #(.addrWidth(24), .dataWidth(32)) rom_1 (.addr(program_counter_1_pc_2), .data(rom_1_data));
  Shifter #(.width(28)) shifter_1 (.in({2'b00, rom_1_data[25:0]}), .\dist (5'b00010), .out(shifter_1_out[27:0]));
  Multiplexer #(.width(32)) multiplexer_6 (
    .in0(multiplexer_12_out), .in1({shifter_1_out[31:28], adder_1_out}), .out(multiplexer_6_out),
    .sel(control_unit_extended_1_jumpandlink));
  // Probe on multiplexer_9_out
  // Probe on multiplexer_6_out
  assign bit_extender_1_out = {{27{1'b0}}, rom_1_data[10:6]};  // Bit_Extender bit_extender_1
  assign bit_extender_2_out = {{16{rom_1_data[15]}}, rom_1_data[15:0]};  // Bit_Extender bit_extender_2
  Multiplexer #(.width(32)) multiplexer_7 (
    .in0(bit_extender_2_out), .in1(bit_extender_3_out), .out(multiplexer_7_out),
    .sel(control_unit_extended_1_immextend));
  assign bit_extender_3_out = {{16{1'b0}}, rom_1_data[15:0]};  // Bit_Extender bit_extender_3
  Control_Unit_Extended control_unit_extended_1 (
    .Opcode(rom_1_data[31:26]), .Funct(rom_1_data[5:0]), .RegDst(control_unit_extended_1_regdst),
    .ALUSrc(control_unit_extended_1_alusrc), .ImmExtend(control_unit_extended_1_immextend),
    .JumpReg(control_unit_extended_1_jumpreg), .Shift(control_unit_extended_1_shift),
    .MemtoReg(control_unit_extended_1_memtoreg), .MemWrite(control_unit_extended_1_memwrite),
    .Branch(control_unit_extended_1_branch), .BranchNot(control_unit_extended_1_branchnot),
    .Jump(control_unit_extended_1_jump), .JumpandLink(control_unit_extended_1_jumpandlink),
    .RegWrite(control_unit_extended_1_regwrite), .ALUControl(control_unit_extended_1_alucontrol));
  Register_File_Test register_file_test_1 (
    .CLK(clock_1_out), .WE3(control_unit_extended_1_regwrite), .A3(multiplexer_9_out),
    .WD3(multiplexer_6_out), .A1(rom_1_data[25:21]), .A2(rom_1_data[20:16]), .RD1(register_file_test_1_rd1),
    .RD2(register_file_test_1_rd2));
  Multiplexer #(.width(5)) multiplexer_8 (
    .in0(rom_1_data[20:16]), .in1(rom_1_data[15:11]), .out(multiplexer_8_out),
    .sel(control_unit_extended_1_regdst));
  Multiplexer #(.width(5)) multiplexer_9 (
    .in0(multiplexer_8_out), .in1({5{1'b1}}), .out(multiplexer_9_out),
    .sel(control_unit_extended_1_jumpandlink));
  Multiplexer #(.width(32)) multiplexer_10 (
    .in0(register_file_test_1_rd1), .in1(bit_extender_1_out), .out(multiplexer_10_out),
    .sel(control_unit_extended_1_shift));
  Multiplexer #(.width(32)) multiplexer_11 (
    .in0(register_file_test_1_rd2), .in1(multiplexer_7_out), .out(multiplexer_11_out),
    .sel(control_unit_extended_1_alusrc));
  Shifter #(.width(32)) shifter_2 (.in(multiplexer_7_out), .\dist (5'b00010), .out(shifter_2_out));
  Adder #(.width(32)) adder_2 (
    .a(shifter_2_out), .b({shifter_1_out[31:28], adder_1_out}), .out(adder_2_out));  // open: cin, cout
  ALU_32bit alu_32bit_1 (
    .ALUControl(control_unit_extended_1_alucontrol), .SrcA(multiplexer_10_out), .SrcB(multiplexer_11_out),
    .Zero(alu_32bit_1_zero), .ALUResult(alu_32bit_1_aluresult));  // open: Cout
  not not_1 (not_1_out, alu_32bit_1_zero);
  and and_1 (and_1_out, control_unit_extended_1_branchnot, not_1_out);
  and and_2 (and_2_out, control_unit_extended_1_branch, alu_32bit_1_zero);
  Data_Memory data_memory_1 (
    .A(alu_32bit_1_aluresult[25:2]), .WE(control_unit_extended_1_memwrite), .CLK(clock_1_out),
    .WD(register_file_test_1_rd2), .RD(data_memory_1_rd));
  Multiplexer #(.width(32)) multiplexer_12 (
    .in0(alu_32bit_1_aluresult), .in1(data_memory_1_rd), .out(multiplexer_12_out),
    .sel(control_unit_extended_1_memtoreg));

  // Notes on the sheet:
  //   beq-bne-j-jr
endmodule

module play_test (
  input  [25:0] in_1,
  input  in_2,
  input  in_3,
  input  in_4,
  input  [31:0] in_5,
  output [31:0] out_6
);

  wire decoder_1_out0, decoder_1_out1, decoder_1_out2, decoder_1_out3, not_1_out;

  Decoder #(.select(2)) decoder_1 (
    .out0(decoder_1_out0), .out1(decoder_1_out1), .out2(decoder_1_out2), .out3(decoder_1_out3),
    .sel(in_1[1:0]), .en(in_3));
  not not_1 (not_1_out, in_2);
  RAM #(.addrWidth(24), .byteenables("byteEnables"), .dataWidth(32)) ram_1 (
    .addr(in_1[25:2]), .we(in_2), .oe(not_1_out), .clk(in_4), .din(in_5), .dout(out_6), .be3(decoder_1_out0),
    .be2(decoder_1_out1), .be1(decoder_1_out2), .be0(decoder_1_out3));
endmodule
