// Logisim project image_drawer_processor.circ as structural Verilog: 2 circuits, main circuit image_drawer_cpu
module image_drawer_cpu (
  input  in_1
);

  wire alu_32bit_1_zero, and_1_out, and_2_out, and_3_out, clock_1_out, control_unit_extended_1_alusrc,
       control_unit_extended_1_branch, control_unit_extended_1_branchnot, control_unit_extended_1_immextend,
       control_unit_extended_1_jump, control_unit_extended_1_jumpandlink, control_unit_extended_1_jumpreg,
       control_unit_extended_1_memtoreg, control_unit_extended_1_memwrite, control_unit_extended_1_regdst,
       control_unit_extended_1_regwrite, control_unit_extended_1_shift, not_1_out, not_2_out, not_3_out,
       not_4_out, not_5_out, not_6_out, not_7_out, not_8_out;
  wire [4:0] control_unit_extended_1_alucontrol, multiplexer_8_out, multiplexer_9_out;
  wire [10:0] adder_3_out, adder_4_out, rgb_video_1_p4, rgb_video_1_p5;
  wire [27:0] adder_1_out;
  wire [31:0] adder_1_out_2, adder_2_out, alu_32bit_1_aluresult, bit_extender_1_out, bit_extender_2_out,
       bit_extender_3_out, data_memory_1_rd, multiplexer_1_out, multiplexer_2_out, multiplexer_3_out,
       multiplexer_4_out, multiplexer_5_out, multiplexer_6_out, multiplexer_7_out, multiplexer_10_out,
       multiplexer_11_out, multiplexer_12_out, program_counter_1_pc, register_file_test_1_rd1,
       register_file_test_1_rd2, rom_1_data, shifter_2_out;

  Multiplexer #(.width(32)) multiplexer_1 (
    .in0(multiplexer_5_out), .in1({32{1'b0}}), .out(multiplexer_1_out), .sel(in_1));
  Multiplexer #(.width(32)) multiplexer_2 (
    .in0({adder_1_out_2[31:28], adder_1_out}), .in1(adder_2_out), .out(multiplexer_2_out), .sel(and_2_out));
  Multiplexer #(.width(32)) multiplexer_3 (
    .in0(multiplexer_2_out), .in1(adder_2_out), .out(multiplexer_3_out), .sel(and_1_out));
  Multiplexer #(.width(32)) multiplexer_4 (
    .in0(multiplexer_3_out), .in1(adder_1_out_2), .out(multiplexer_4_out), .sel(control_unit_extended_1_jump));
  Multiplexer #(.width(32)) multiplexer_5 (
    .in0(multiplexer_4_out), .in1(register_file_test_1_rd1), .out(multiplexer_5_out),
    .sel(control_unit_extended_1_jumpreg));
  Clock clock_1 (.out(clock_1_out));
  Adder #(.width(32)) adder_1 (
    .a(program_counter_1_pc), .b(32'h4), .out({adder_1_out_2[31:28], adder_1_out}));  // open: cin, cout
  // Probe on program_counter_1_pc
  Program_Counter program_counter_1 (.CLK(clock_1_out), .PCp(multiplexer_1_out), .PC(program_counter_1_pc));
  ROM #(.addrWidth(24), .dataWidth(32)) rom_1 (.addr(program_counter_1_pc[25:2]), .data(rom_1_data));
  Shifter #(.width(28)) shifter_1 (.in({2'b00, rom_1_data[25:0]}), .\dist (5'b00010), .out(adder_1_out_2[27:0]));
  Multiplexer #(.width(32)) multiplexer_6 (
    .in0(multiplexer_12_out), .in1({adder_1_out_2[31:28], adder_1_out}), .out(multiplexer_6_out),
    .sel(control_unit_extended_1_jumpandlink));
  // Probe on multiplexer_9_out
  // Probe on multiplexer_6_out
  assign bit_extender_1_out = {{27{1'b0}}, rom_1_data[10:6]};  // Bit_Extender bit_extender_1
  assign bit_extender_2_out = {{16{rom_1_data[15]}}, rom_1_data[15:0]};  // Bit_Extender bit_extender_2
  Multiplexer #(.width(32)) multiplexer_7 (
    .in0(bit_extender_2_out), .in1(bit_extender_3_out), .out(multiplexer_7_out),
    .sel(control_unit_extended_1_immextend));
  assign bit_extender_3_out = {{16{1'b0}}, rom_1_data[15:0]};  // Bit_Extender bit_extender_3
  Control_Unit_Extended control_unit_extended_1 (
    .Opcode(rom_1_data[31:26]), .Funct(rom_1_data[5:0]), .RegDst(control_unit_extended_1_regdst),
    .ALUSrc(control_unit_extended_1_alusrc), .ImmExtend(control_unit_extended_1_immextend),
    .JumpReg(control_unit_extended_1_jumpreg), .Shift(control_unit_extended_1_shift),
    .MemtoReg(control_unit_extended_1_memtoreg), .MemWrite(control_unit_extended_1_memwrite),
    .Branch(control_unit_extended_1_branch), .BranchNot(control_unit_extended_1_branchnot),
    .Jump(control_unit_extended_1_jump), .JumpandLink(control_unit_extended_1_jumpandlink),
    .RegWrite(control_unit_extended_1_regwrite), .ALUControl(control_unit_extended_1_alucontrol));
  Register_File_Test register_file_test_1 (
    .CLK(clock_1_out), .WE3(control_unit_extended_1_regwrite), .A3(multiplexer_9_out),
    .WD3(multiplexer_6_out), .A1(rom_1_data[25:21]), .A2(rom_1_data[20:16]), .RD1(register_file_test_1_rd1),
    .RD2(register_file_test_1_rd2));
  Multiplexer #(.width(5)) multiplexer_8 (
    .in0(rom_1_data[20:16]), .in1(rom_1_data[15:11]), .out(multiplexer_8_out),
    .sel(control_unit_extended_1_regdst));
  Multiplexer #(.width(5)) multiplexer_9 (
    .in0(multiplexer_8_out), .in1({5{1'b1}}), .out(multiplexer_9_out),
    .sel(control_unit_extended_1_jumpandlink));
  Multiplexer #(.width(32)) multiplexer_10 (
    .in0(register_file_test_1_rd1), .in1(bit_extender_1_out), .out(multiplexer_10_out),
    .sel(control_unit_extended_1_shift));
  Multiplexer #(.width(32)) multiplexer_11 (
    .in0(register_file_test_1_rd2), .in1(multiplexer_7_out), .out(multiplexer_11_out),
    .sel(control_unit_extended_1_alusrc));
  Shifter #(.width(32)) shifter_2 (.in(multiplexer_7_out), .\dist (5'b00010), .out(shifter_2_out));
  ALU_32bit alu_32bit_1 (
    .ALUControl(control_unit_extended_1_alucontrol), .SrcA(multiplexer_10_out), .SrcB(multiplexer_11_out),
    .Zero(alu_32bit_1_zero), .ALUResult(alu_32bit_1_aluresult));  // open: Cout
  Adder #(.width(32)) adder_2 (
    .a(shifter_2_out), .b({adder_1_out_2[31:28], adder_1_out}), .out(adder_2_out));  // open: cin, cout
  not not_1 (not_1_out, alu_32bit_1_zero);
  and and_1 (and_1_out, control_unit_extended_1_branchnot, not_1_out);
  and and_2 (and_2_out, control_unit_extended_1_branch, alu_32bit_1_zero);
  Data_Memory data_memory_1 (
    .A(alu_32bit_1_aluresult[25:2]), .WE(control_unit_extended_1_memwrite), .CLK(clock_1_out),
    .WD(register_file_test_1_rd2), .RD(data_memory_1_rd));
  Multiplexer #(.width(32)) multiplexer_12 (
    .in0(alu_32bit_1_aluresult), .in1(data_memory_1_rd), .out(multiplexer_12_out),
    .sel(control_unit_extended_1_memtoreg));
  // RGB_Video #(.height(1080), .width(1920)) rgb_video_1: pin names not known; wires that end beside it: 1'b0, clock_1_out, control_unit_extended_1_memtoreg, rgb_video_1_p4, rgb_video_1_p5, multiplexer_12_out[23:0]
  Register #(.width(11)) register_1 (
    .D(adder_3_out), .en(1'b1), .clk(control_unit_extended_1_memtoreg), .Q(rgb_video_1_p4), .clr(and_3_out));
  Adder #(.width(11)) adder_3 (.a(rgb_video_1_p4), .b(11'h1), .out(adder_3_out));  // open: cin, cout
  not not_2 (not_2_out, rgb_video_1_p4[0]);
  not not_3 (not_3_out, rgb_video_1_p4[1]);
  not not_4 (not_4_out, rgb_video_1_p4[2]);
  not not_5 (not_5_out, rgb_video_1_p4[3]);
  not not_6 (not_6_out, rgb_video_1_p4[4]);
  not not_7 (not_7_out, rgb_video_1_p4[5]);
  not not_8 (not_8_out, rgb_video_1_p4[6]);
  and and_3 (and_3_out, not_2_out, not_3_out, not_4_out, not_5_out, not_6_out, not_7_out, not_8_out, rgb_video_1_p4[7], rgb_video_1_p4[8], rgb_video_1_p4[9], rgb_video_1_p4[10]);
  Register #(.trigger("high"), .width(11)) register_2 (
    .D(adder_4_out), .en(and_3_out), .clk(control_unit_extended_1_memtoreg), .Q(rgb_video_1_p5));  // open: clr
  Adder #(.width(11)) adder_4 (.a(rgb_video_1_p5), .b(11'h1), .out(adder_4_out));  // open: cin, cout

  // Notes on the sheet:
  //   beq-bne-j-jr
  //   contents of rom_1 (hex, n*v repeats v):
  //   20080000 2012a400 11120003 8d100000 21080004 8000002 8000006
endmodule

module image_drawer_without_cpu (
);

  wire and_1_out, clock_1_out, not_1_out, not_2_out, not_3_out, not_4_out, not_5_out, not_6_out, not_7_out;
  wire [10:0] adder_2_out, adder_3_out, register_2_q, rgb_video_1_p5;
  wire [23:0] adder_1_out, register_1_q;
  wire [31:0] rom_1_data;

  Clock clock_1 (.out(clock_1_out));
  Register #(.width(24)) register_1 (.D(adder_1_out), .en(1'b1), .clk(clock_1_out), .Q(register_1_q));  // open: clr
  Adder #(.width(24)) adder_1 (.a(register_1_q), .b(24'h1), .out(adder_1_out));  // open: cin, cout
  ROM #(.addrWidth(24), .dataWidth(32)) rom_1 (.addr(register_1_q), .data(rom_1_data));
  Register #(.width(11)) register_2 (.D(adder_2_out), .en(1'b1), .clk(clock_1_out), .Q(register_2_q), .clr(and_1_out));
  // RGB_Video #(.height(1080), .width(1920)) rgb_video_1: pin names not known; wires that end beside it: 1'b0, clock_1_out, clock_1_out, register_2_q, rgb_video_1_p5, rom_1_data[23:0]
  Adder #(.width(11)) adder_2 (.a(register_2_q), .b(11'h1), .out(adder_2_out));  // open: cin, cout
  not not_1 (not_1_out, register_2_q[0]);
  not not_2 (not_2_out, register_2_q[1]);
  not not_3 (not_3_out, register_2_q[2]);
  not not_4 (not_4_out, register_2_q[3]);
  not not_5 (not_5_out, register_2_q[4]);
  not not_6 (not_6_out, register_2_q[5]);
  not not_7 (not_7_out, register_2_q[6]);
  and and_1 (and_1_out, not_1_out, not_2_out, not_3_out, not_4_out, not_5_out, not_6_out, not_7_out, register_2_q[7], register_2_q[8], register_2_q[9], register_2_q[10]);
  Register #(.trigger("high"), .width(11)) register_3 (
    .D(adder_3_out), .en(and_1_out), .clk(clock_1_out), .Q(rgb_video_1_p5));  // open: clr
  Adder #(.width(11)) adder_3 (.a(rgb_video_1_p5), .b(11'h1), .out(adder_3_out));  // open: cin, cout

  // Notes on the sheet:
  //   contents of rom_1 (hex, n*v repeats v):
  //   224563 224563 234561 244861 254760 234562 234463 224461 234561 234561 234660 264863 264863 244661
  //   244661 234560 224660 234861 224761 264863 2a4964 2c4964 2c4a64 2b4a66 2c4b66 314c65 344e64 385065
  //   3a5165 3b5065 3f5266 405467 415265 405266 405266 405266 3f5165 4*405266 405166 3f5164 3e5163 3d4f64
  //   3a4e63 364f65 345066 344e62 334e62 314d62 2e4b62 2c4a63 294961 264961 254962 234864 204664 1d4463
  //   1c4561 1b4561 1c4760 204761 234762 234863 224762 214663 224764 214663 214564 204464 1d4362 1c4563
  //   1a4563 1a4563 1d4664 1d4664 1c4563 1b4463 4*1c4563 1d4664 1c4563 1c4563 1c4563 1d4664 1e4765 1e4866
  //   1e4765 1f4564 1d4464 1e4565 1d4664 1d4664 1c4563 4*1d4664 1a4562 184461 194562 5*1a4663 1b4764
  //   1b4764 1a4663 1b4764 1a4663 1a4663 1a4663 1b4764 1c4663 1c4563 1c4563 1c4563 1c4562 1c4663 1c4865
  //   1a4663 1a4663 1a4663 1b4764 194665 4*184564 194665 194665 194665 184564 184564 184564 184565 194665
  //   1a4765 1a4863 1a4762 194666 194667 194666 184564 184564 194666 194667 184566 1a4768 194667 184566
  //   5*184667 174566 4*184667 174566 174566 174566 184667 174566 174566 174566 7*184667 194667 194667
  //   184667 184667 4*174566 184667 184667 174566 184667 184667 174566 164465 164465 174566 164465 174566
  //   194767 1a4665 184564 1a4664 1c4664 1d4664 1f4866 1e4765 1d4664 1d4664 1c4665 1a4666 194665 194666
  //   174465 194668 184668 174566 174663 184764 1b4763 1e4662 1e4763 1e4763 1d4863 1c4864 184667 184667
  //   7*174566 4*184667 194768 194768 9*184667 174566 184667 174566 184667 184667 184667 184566 174465
  //   184667 174566 6*184667 174566 174566 174566 164465 174566 184667 184667 184667 11*174566 184667
  //   174566 184667 184667 174566 184667 184667 164465 174566 174566 174566 184667 4*174566 184667 174566
  //   5*184667 4*174566 184667 184667 184667 174566 174566 174566 184667 184667 184667 174566 174566
  //   4*184667 4*174566 5*184667 194768 184667 174566 6*184667 174566 174566 1a4768 194667 194667 184667
  //   164767 154867 144867 184868 154867 154867 154867 174767 184667 184667 184667 5*194768 1a4869 184667
  //   17*194768 1a4768 194768 184767 164767 154867 154867 154867 144766 144766 144867 164767 194768 194768
  //   194768 184667 184667 184667 194768 194768 184667 184667 4*194768 184667 184667 8*194768 184667
  //   194667 164767 154867 164767 184868 194768 194768 184566 174767 154867 154867 154867 164968 154867
  //   144766 144766 144766 5*154867 164968 4*154867 164968 164968 164968 174868 184768 4*194768 184667
  //   184667 194667 1a4768 194768 194667 194768 184869 5*174868 154867 154867 154867 164968 154867 154867
  //   164968 164968 7*154867 164968 154867 154867 154867 144766 144766 144766 154867 154867 144766 144766
  //   154867 154867 144766 154867 164968 164968 154867 154867 6*164968 174a69 164968 154867 154867
  //   7*164968 174a69 174a69 174a69 164968 164968 174a69 174a69 4*164968 174a69 174a69 164a69 174a69
  //   184869 1a4869 1b4869 1a4869 174a69 174a69 4*164968 174a69 164968 164968 164968 154867 154867
  //   5*164968 174a69 164968 174a69 164968 174a69 174a69 174a69 164968 164968 164968 4*174a69 164968
  //   174a69 164968 164968 164968 174a69 5*164968 174a69 174a69 174a69 164968 164968 164968 174a69 164968
  //   154867 154867 174a69 154867 4*164968 154867 164968 154867 164968 154867 154867 164968 164968 154867
  //   164968 184b6a 5*174a69 164968 154867 164968 174a69 174a69 164968 154867 154867 6*164968 5*174a69
  //   4*164968 174a69 164968 164968 174a69 5*164968 174a69 174a69 164968 174a69 174a69 174a69 164968
  //   164968 6*174a69 184b6a 184b6a 174a69 174a69 174a69 8*184b6a 194c6b 194c6b 194c6b 184b6a 6*194c6b
  //   184c6b 184c6b 194c6b 1b4a6b 1c4a6b 1c496a 194c6b 194c6b 194c6b 184b6a 4*194c6b 184b6a 4*194c6b
  //   184b6a 184b6a 184b6a 4*194c6b 6*1a4d6c 1b4e6d 5*1a4d6c 5*194c6b 4*184b6a 4*194c6b 184b6a 184b6a
  //   4*194c6b 4*1a4d6c 194c6b 1a4d6c 1a4d6c 1a4d6c 5*194c6b 1b4e6d 1b4e6d 1a4d6c 1a4d6c 1a4d6c 1b4e6d
  //   194c6b 1a4d6c 1b4e6d 5*1a4d6c 194c6b 1b4e6d 1a4d6c 1a4d6c 1a4d6c 4*1b4e6d 1a4d6c 1b4e6d 194c6b
  //   1a4d6c 1b4e6d 1b4e6d 1a4d6c 194c6b 194c6b 14*1b4e6d 1a4d6c 1a4d6c 1b4e6d 4*1a4d6c 1b4e6d 1b4e6d
  //   1b4e6d 1a4d6c 1a4d6c 1a4d6c 194c6b 194c6b 1a4d6c 1a4d6c 1a4d6c 1b4e6d 1b4e6d 1b4e6d 1a4d6c 1a4d6c
  //   1c4f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
endmodule
