// Logisim project snake_game_processor.circ as structural Verilog: 3 circuits, main circuit main
module main (
  input  in_1
);

  wire alu_32bit_1_zero, and_1_out, and_2_out, and_3_out, and_4_out, and_5_out, and_6_out, and_7_out,
       and_8_out, C_out, clock_1_out, control_unit_extended_1_alusrc, control_unit_extended_1_branch,
       control_unit_extended_1_branchnot, control_unit_extended_1_immextend, control_unit_extended_1_jump,
       control_unit_extended_1_jumpandlink, control_unit_extended_1_jumpreg,
       control_unit_extended_1_memtoreg, control_unit_extended_1_memwrite, control_unit_extended_1_regdst,
       control_unit_extended_1_regwrite, control_unit_extended_1_shift, keyboard_1_avail,
       memory_address_decoder_1_kbd_status_sel, memory_address_decoder_1_sel_ram,
       memory_address_decoder_1_sel_vid, nor_1_out, nor_2_out, not_1_out, not_2_out, not_3_out, not_4_out,
       not_5_out, not_6_out, not_7_out, not_8_out, Y_out;
  wire [0:0] or_1_out;
  wire [1:0] alu_32bit_1_aluresult, alu_32bit_1_aluresult_3, program_counter_1_pc;
  wire [4:0] control_unit_extended_1_alucontrol, multiplexer_8_out, multiplexer_9_out, register_1_q,
       register_2_q;
  wire [5:0] alu_32bit_1_aluresult_4, program_counter_1_pc_3;
  wire [6:0] keyboard_1_data;
  wire [23:0] alu_32bit_1_aluresult_2, program_counter_1_pc_2;
  wire [27:0] adder_1_out;
  wire [31:0] adder_2_out, bit_extender_1_out, bit_extender_2_out, bit_extender_3_out, bit_extender_4_out,
       bit_extender_5_out, data_memory_1_rd, multiplexer_1_out, multiplexer_2_out, multiplexer_3_out,
       multiplexer_4_out, multiplexer_5_out, multiplexer_6_out, multiplexer_7_out, multiplexer_10_out,
       multiplexer_11_out, multiplexer_12_out, multiplexer_13_out, multiplexer_14_out,
       register_file_test_1_rd1, register_file_test_1_rd2, rom_1_data, shifter_1_out, shifter_2_out;

  Multiplexer #(.width(32)) multiplexer_1 (
    .in0(multiplexer_5_out), .in1({32{1'b0}}), .out(multiplexer_1_out), .sel(in_1));
  Multiplexer #(.width(32)) multiplexer_2 (
    .in0({shifter_1_out[31:28], adder_1_out}), .in1(adder_2_out), .out(multiplexer_2_out), .sel(and_2_out));
  Multiplexer #(.width(32)) multiplexer_3 (
    .in0(multiplexer_2_out), .in1(adder_2_out), .out(multiplexer_3_out), .sel(and_1_out));
  Multiplexer #(.width(32)) multiplexer_4 (
    .in0(multiplexer_3_out), .in1(shifter_1_out), .out(multiplexer_4_out), .sel(control_unit_extended_1_jump));
  Multiplexer #(.width(32)) multiplexer_5 (
    .in0(multiplexer_4_out), .in1(register_file_test_1_rd1), .out(multiplexer_5_out),
    .sel(control_unit_extended_1_jumpreg));
  Clock clock_1 (.out(clock_1_out));
  Adder #(.width(32)) adder_1 (
    .a({program_counter_1_pc_3, program_counter_1_pc_2, program_counter_1_pc}), .b(32'h4),
    .out({shifter_1_out[31:28], adder_1_out}));  // open: cin, cout
  // Probe on {program_counter_1_pc_3, program_counter_1_pc_2, program_counter_1_pc}
  Program_Counter program_counter_1 (
    .CLK(clock_1_out), .PCp(multiplexer_1_out),
    .PC({program_counter_1_pc_3, program_counter_1_pc_2, program_counter_1_pc}));
  ROM #(.addrWidth(24), .dataWidth(32)) rom_1 (.addr(program_counter_1_pc_2), .data(rom_1_data));
  Shifter #(.width(28)) shifter_1 (.in({2'b00, rom_1_data[25:0]}), .\dist (5'b00010), .out(shifter_1_out[27:0]));
  Multiplexer #(.width(32)) multiplexer_6 (
    .in0(multiplexer_14_out), .in1({shifter_1_out[31:28], adder_1_out}), .out(multiplexer_6_out),
    .sel(control_unit_extended_1_jumpandlink));
  assign bit_extender_1_out = {{27{1'b0}}, rom_1_data[10:6]};  // Bit_Extender bit_extender_1
  assign bit_extender_2_out = {{16{rom_1_data[15]}}, rom_1_data[15:0]};  // Bit_Extender bit_extender_2
  Multiplexer #(.width(32)) multiplexer_7 (
    .in0(bit_extender_2_out), .in1(bit_extender_3_out), .out(multiplexer_7_out),
    .sel(control_unit_extended_1_immextend));
  assign bit_extender_3_out = {{16{1'b0}}, rom_1_data[15:0]};  // Bit_Extender bit_extender_3
  Control_Unit_Extended control_unit_extended_1 (
    .Opcode(rom_1_data[31:26]), .Funct(rom_1_data[5:0]), .RegDst(control_unit_extended_1_regdst),
    .ALUSrc(control_unit_extended_1_alusrc), .ImmExtend(control_unit_extended_1_immextend),
    .JumpReg(control_unit_extended_1_jumpreg), .Shift(control_unit_extended_1_shift),
    .MemtoReg(control_unit_extended_1_memtoreg), .MemWrite(control_unit_extended_1_memwrite),
    .Branch(control_unit_extended_1_branch), .BranchNot(control_unit_extended_1_branchnot),
    .Jump(control_unit_extended_1_jump), .JumpandLink(control_unit_extended_1_jumpandlink),
    .RegWrite(control_unit_extended_1_regwrite), .ALUControl(control_unit_extended_1_alucontrol));
  Register_File_Test register_file_test_1 (
    .CLK(clock_1_out), .WE3(control_unit_extended_1_regwrite), .A3(multiplexer_9_out),
    .WD3(multiplexer_6_out), .A1(rom_1_data[25:21]), .A2(rom_1_data[20:16]), .RD1(register_file_test_1_rd1),
    .RD2(register_file_test_1_rd2));
  Multiplexer #(.width(5)) multiplexer_8 (
    .in0(rom_1_data[20:16]), .in1(rom_1_data[15:11]), .out(multiplexer_8_out),
    .sel(control_unit_extended_1_regdst));
  Multiplexer #(.width(5)) multiplexer_9 (
    .in0(multiplexer_8_out), .in1({5{1'b1}}), .out(multiplexer_9_out),
    .sel(control_unit_extended_1_jumpandlink));
  Multiplexer #(.width(32)) multiplexer_10 (
    .in0(register_file_test_1_rd1), .in1(bit_extender_1_out), .out(multiplexer_10_out),
    .sel(control_unit_extended_1_shift));
  Multiplexer #(.width(32)) multiplexer_11 (
    .in0(register_file_test_1_rd2), .in1(multiplexer_7_out), .out(multiplexer_11_out),
    .sel(control_unit_extended_1_alusrc));
  Shifter #(.width(32)) shifter_2 (.in(multiplexer_7_out), .\dist (5'b00010), .out(shifter_2_out));
  Adder #(.width(32)) adder_2 (
    .a(shifter_2_out), .b({shifter_1_out[31:28], adder_1_out}), .out(adder_2_out));  // open: cin, cout
  ALU_32bit alu_32bit_1 (
    .ALUControl(control_unit_extended_1_alucontrol), .SrcA(multiplexer_10_out), .SrcB(multiplexer_11_out),
    .Zero(alu_32bit_1_zero),
    .ALUResult({alu_32bit_1_aluresult_4, alu_32bit_1_aluresult_2[23:12], alu_32bit_1_aluresult_3, alu_32bit_1_aluresult_2[9:0], alu_32bit_1_aluresult}));  // open: Cout
  not not_1 (not_1_out, alu_32bit_1_zero);
  and and_1 (and_1_out, control_unit_extended_1_branchnot, not_1_out);
  and and_2 (and_2_out, control_unit_extended_1_branch, alu_32bit_1_zero);
  and and_3 (and_3_out, control_unit_extended_1_memtoreg, memory_address_decoder_1_sel_ram);
  // Probe on {alu_32bit_1_aluresult_4, alu_32bit_1_aluresult_2[23:12], alu_32bit_1_aluresult_3, alu_32bit_1_aluresult_2[9:0], alu_32bit_1_aluresult}
  and and_4 (and_4_out, memory_address_decoder_1_kbd_status_sel, control_unit_extended_1_memtoreg);
  not not_2 (not_2_out, alu_32bit_1_aluresult_2[0]);
  not not_3 (not_3_out, alu_32bit_1_aluresult_2[1]);
  not not_4 (not_4_out, alu_32bit_1_aluresult_2[1]);
  not not_5 (not_5_out, alu_32bit_1_aluresult_2[0]);
  Keyboard keyboard_1 (.clk(clock_1_out), .re(and_4_out), .clr(1'b0), .avail(keyboard_1_avail), .data(keyboard_1_data));
  and and_5 (and_5_out, memory_address_decoder_1_sel_vid, not_2_out, not_3_out);
  and Y (Y_out, memory_address_decoder_1_sel_vid, alu_32bit_1_aluresult_2[0], not_4_out);
  and C (C_out, memory_address_decoder_1_sel_vid, not_5_out, alu_32bit_1_aluresult_2[1]);
  memory_address_decoder memory_address_decoder_1 (
    .address_2(alu_32bit_1_aluresult_2[0]), .Select_bits(alu_32bit_1_aluresult_3),
    .sel_ram(memory_address_decoder_1_sel_ram), .sel_vid(memory_address_decoder_1_sel_vid),
    .kbd_status_sel(memory_address_decoder_1_kbd_status_sel));  // open: kbd_data_sel, sel_keyboard, sel_unused
  Data_Memory data_memory_1 (
    .A({alu_32bit_1_aluresult_2[23:12], alu_32bit_1_aluresult_3, alu_32bit_1_aluresult_2[9:0]}),
    .WE(control_unit_extended_1_memwrite), .CLK(clock_1_out), .WD(register_file_test_1_rd2),
    .RD(data_memory_1_rd));
  Register #(.width(5)) register_1 (
    .D(register_file_test_1_rd2[4:0]), .en(and_6_out), .clk(clock_1_out), .Q(register_1_q));  // open: clr
  and and_6 (and_6_out, control_unit_extended_1_memwrite, and_5_out);
  Register #(.width(5)) register_2 (
    .D(register_file_test_1_rd2[4:0]), .en(and_7_out), .clk(clock_1_out), .Q(register_2_q));  // open: clr
  and and_7 (and_7_out, control_unit_extended_1_memwrite, Y_out);
  and and_8 (and_8_out, control_unit_extended_1_memwrite, C_out);
  assign bit_extender_4_out = {{31{1'b0}}, keyboard_1_avail};  // Bit_Extender bit_extender_4
  assign bit_extender_5_out = {{25{1'b0}}, keyboard_1_data};  // Bit_Extender bit_extender_5
  // RGB_Video #(.height(32), .scale(8), .width(32)) rgb_video_1: pin names not known; wires that end beside it: 1'b0, clock_1_out, and_8_out, register_1_q, register_2_q, register_file_test_1_rd2[23:0]
  Multiplexer #(.width(32)) multiplexer_12 (
    .in0(bit_extender_4_out), .in1(bit_extender_5_out), .out(multiplexer_12_out),
    .sel(alu_32bit_1_aluresult_2[0]));
  Multiplexer #(.width(32)) multiplexer_13 (
    .in0({alu_32bit_1_aluresult_4, alu_32bit_1_aluresult_2[23:12], alu_32bit_1_aluresult_3, alu_32bit_1_aluresult_2[9:0], alu_32bit_1_aluresult}),
    .in1(data_memory_1_rd), .out(multiplexer_13_out), .sel(control_unit_extended_1_memtoreg));
  Multiplexer #(.select(2), .width(32)) multiplexer_14 (
    .in0(multiplexer_13_out), .in1(multiplexer_12_out), .out(multiplexer_14_out), .sel({1'b0, or_1_out[0]}));  // open: in2, in3
  not not_6 (not_6_out, alu_32bit_1_aluresult_2[0]);
  not not_7 (not_7_out, alu_32bit_1_aluresult_3[0]);
  not not_8 (not_8_out, alu_32bit_1_aluresult_3[0]);
  nor nor_1 (nor_1_out, alu_32bit_1_aluresult_3[1], alu_32bit_1_aluresult[0], alu_32bit_1_aluresult[1], not_6_out, alu_32bit_1_aluresult_2[1], alu_32bit_1_aluresult_2[2], alu_32bit_1_aluresult_2[3], alu_32bit_1_aluresult_2[4], alu_32bit_1_aluresult_2[5], alu_32bit_1_aluresult_2[6], alu_32bit_1_aluresult_2[7], alu_32bit_1_aluresult_2[8], alu_32bit_1_aluresult_2[9], not_7_out, alu_32bit_1_aluresult_2[12], alu_32bit_1_aluresult_2[13], alu_32bit_1_aluresult_2[14], alu_32bit_1_aluresult_2[15], alu_32bit_1_aluresult_2[16], alu_32bit_1_aluresult_2[17], alu_32bit_1_aluresult_2[18], alu_32bit_1_aluresult_2[19], alu_32bit_1_aluresult_2[20], alu_32bit_1_aluresult_2[21], alu_32bit_1_aluresult_2[22], alu_32bit_1_aluresult_2[23], alu_32bit_1_aluresult_4[0], alu_32bit_1_aluresult_4[1], alu_32bit_1_aluresult_4[2], alu_32bit_1_aluresult_4[3], alu_32bit_1_aluresult_4[4], alu_32bit_1_aluresult_4[5]);
  nor nor_2 (nor_2_out, alu_32bit_1_aluresult_3[1], alu_32bit_1_aluresult[0], alu_32bit_1_aluresult[1], alu_32bit_1_aluresult_2[0], alu_32bit_1_aluresult_2[1], alu_32bit_1_aluresult_2[2], alu_32bit_1_aluresult_2[3], alu_32bit_1_aluresult_2[4], alu_32bit_1_aluresult_2[5], alu_32bit_1_aluresult_2[6], alu_32bit_1_aluresult_2[7], alu_32bit_1_aluresult_2[8], alu_32bit_1_aluresult_2[9], not_8_out, alu_32bit_1_aluresult_2[12], alu_32bit_1_aluresult_2[13], alu_32bit_1_aluresult_2[14], alu_32bit_1_aluresult_2[15], alu_32bit_1_aluresult_2[16], alu_32bit_1_aluresult_2[17], alu_32bit_1_aluresult_2[18], alu_32bit_1_aluresult_2[19], alu_32bit_1_aluresult_2[20], alu_32bit_1_aluresult_2[21], alu_32bit_1_aluresult_2[22], alu_32bit_1_aluresult_2[23], alu_32bit_1_aluresult_4[0], alu_32bit_1_aluresult_4[1], alu_32bit_1_aluresult_4[2], alu_32bit_1_aluresult_4[3], alu_32bit_1_aluresult_4[4], alu_32bit_1_aluresult_4[5]);
  or or_1 (or_1_out[0], nor_1_out, nor_2_out);

  // Notes on the sheet:
  //   beq-bne-j-jr
  //   contents of rom_1 (hex, n*v repeats v):
  //   20100003 20110001 20120000 20160005 20170010 20080005 ac080000 20080010 ac080004 20080004 ac080008
  //   20080010 ac08000c 20080003 ac080010 20080010 ac080014 20153039 c000091 200c0000 200d0000 340eff00
  //   11900007 8da40000 8da50004 1c03020 c000067 218c0001 21ad0008 8000016 c000079 2d14020 3108001f
  //   2f24820 3129001f 100b020 120b820 2c02020 2e02820 c00006b 14400030 200a0000 16d30002 16f40001
  //   200a0001 1140000f 200b01e0 120b000d 8000031 2005820 11600008 b60c0 218dfff8 8dae0000 8daf0004
  //   ad8e0000 ad8f0004 216bffff 8000032 22100001 800004f 220bffff b60c0 8d980000 8d990004 11600008 b60c0
  //   218dfff8 8dae0000 8daf0004 ad8e0000 ad8f0004 216bffff 8000041 3002020 3202820 20060000 c000067
  //   800004f ac160000 ac170004 2c02020 2e02820 3406ff00 c000067 11400001 c000091 c0000ab 800001e 200d0020
  //   20080000 110d000a 20090000 112d0006 1202020 1002820 3c0600ff c000067 21290001 800005d 21080001
  //   800005b 8000066 ac042000 ac052004 ac062008 3e00008 20080000 20090000 11100009 8d2a0000 8d2b0004
  //   15440003 15650002 20020001 3e00008 21080001 21290008 800006d 20020000 3e00008 8c081000 11000015
  //   8c091004 200a0077 152a0003 20110000 2012ffff 8000079 200a0061 152a0003 2011ffff 20120000 8000079
  //   200a0073 152a0003 20110000 20120001 8000079 200a0064 152affec 20110001 20120000 8000079 3e00008
  //   ac1f0f3c 20190014 154340 2a8a826 154442 2a8a826 154140 2a8a826 32ac001f 156942 31ad001f 1802020
  //   1a02820 c00006b 10400003 2339ffff 13200001 8000093 1809820 1a0a020 2602020 2802820 3c0600ff c000067
  //   8c1f0f3c 3e00008 20080005 11000002 2108ffff 80000ac 3e00008
  //   X
endmodule

module play_test (
  input  in_1,
  input  in_2,
  input  in_3,
  input  [4:0] in_4,
  input  [4:0] in_5,
  output [6:0] out_6,
  output out_7
);

  wire clock_1_out;

  // RGB_Video #(.height(32), .scale(8), .width(32)) rgb_video_1: pin names not known; wires that end beside it: in_2, in_3, in_4, in_5, 24'hff0000
  Clock clock_1 (.out(clock_1_out));
  Keyboard keyboard_1 (.clk(clock_1_out), .re(in_1), .avail(out_7), .data(out_6));  // open: clr
endmodule

module memory_address_decoder (
  input  address_2,
  input  [1:0] Select_bits,
  output kbd_data_sel,
  output sel_ram,
  output sel_keyboard,
  output sel_vid,
  output kbd_status_sel,
  output sel_unused
);

  wire not_1_out;

  Decoder #(.enable("false"), .select(2)) decoder_1 (
    .out0(sel_ram), .out1(sel_keyboard), .out2(sel_vid), .out3(sel_unused), .sel(Select_bits));
  and and_1 (kbd_data_sel, address_2, sel_keyboard);
  and and_2 (kbd_status_sel, sel_keyboard, not_1_out);
  not not_1 (not_1_out, address_2);
endmodule
